// Logisim project mini_chip8_alu1.circ as structural Verilog: 11 circuits, main circuit ALU1
module ALU1 (
  input  [11:0] saut,
  input  [11:0] NNN,
  input  [11:0] PC,
  input  [3:0] nbrsaut,
  input  [3:0] X,
  input  [7:0] VX,
  input  [7:0] KK,
  input  [3:0] Y,
  input  [7:0] VY,
  input  _0NNN,
  input  _00E0,
  input  _00EE,
  input  _1NNN,
  input  _2NNN,
  input  _3XKK,
  input  _4XKK,
  input  _5XY0,
  input  _6XKK,
  input  _7XKK,
  input  H,
  input  T1,
  input  T2,
  output RE,
  output [11:0] PC_2,
  output SPC,
  output Snbrsaut,
  output [3:0] nbrsaut_2,
  output [11:0] saut_2,
  output Ssaut,
  output [3:0] AX,
  output [3:0] AY,
  output [7:0] VX_2,
  output SVX,
  output EC,
  output [3:0] NC
);

  wire n00e0_1_ec, n00ee_1_ec, n00ee_1_snbrsaut, n00ee_1_spc, n0nnn_1_ec, n1nnn_1_ec, n1nnn_1_spc,
       n2nnn_1_ec, n2nnn_1_snbrsaut, n2nnn_1_spc, n3xnn_1_ec, n3xnn_1_spc, n4xkk_1_ec, n4xkk_1_spc,
       n5xy0_1_ec, n5xy0_1_spc, n6xkk_1_ec, n6xkk_1_svx, n7xkk_1_ec, n7xkk_1_svx, or_2_out;
  wire [3:0] n00e0_1_nc, n00ee_1_nbrsaut_2, n00ee_1_nc, n0nnn_1_nc, n1nnn_1_nc, n2nnn_1_nbrsaut_2,
       n2nnn_1_nc, n3xnn_1_ax, n3xnn_1_nc, n4xkk_1_ax, n4xkk_1_nc, n5xy0_1_ax, n5xy0_1_nc, n6xkk_1_ax,
       n6xkk_1_nc, n7xkk_1_ax, n7xkk_1_nc;
  wire [7:0] n6xkk_1_vx, n7xkk_1_vx_2;
  wire [11:0] n00ee_1_pc, n1nnn_1_pc, n2nnn_1_pc_2, n3xnn_1_pc_2, n4xkk_1_pc_2, n5xy0_1_pc_2, or_1_out;

  _3XNN u_3xnn_1 (
    .VX(VX), .KK(KK), .PC(PC), .PC_2(n3xnn_1_pc_2), .SPC(n3xnn_1_spc), .X(X), .AX(n3xnn_1_ax),
    .EC(n3xnn_1_ec), .T1(T1), .NC(n3xnn_1_nc), .enable(_3XKK), .H(H));
  _4XKK u_4xkk_1 (
    .VX(VX), .KK(KK), .PC(PC), .PC_2(n4xkk_1_pc_2), .SPC(n4xkk_1_spc), .X(X), .AX(n4xkk_1_ax),
    .EC(n4xkk_1_ec), .T1(T1), .NC(n4xkk_1_nc), .enable(_4XKK), .H(H));
  _5XY0 u_5xy0_1 (
    .VX(VX), .VY(VY), .PC(PC), .PC_2(n5xy0_1_pc_2), .SPC(n5xy0_1_spc), .X(X), .AX(n5xy0_1_ax), .Y(Y),
    .AY(AY), .EC(n5xy0_1_ec), .T1(T1), .NC(n5xy0_1_nc), .enable(_5XY0), .H(H));
  _0NNN u_0nnn_1 (.enable(_0NNN), .EC(n0nnn_1_ec), .NC(n0nnn_1_nc));
  _00EE u_00ee_1 (
    .nbrsaut(nbrsaut), .saut(saut), .nbrsaut_2(n00ee_1_nbrsaut_2), .Snbrsaut(n00ee_1_snbrsaut),
    .PC(n00ee_1_pc), .SPC(n00ee_1_spc), .EC(n00ee_1_ec), .T2(T2), .NC(n00ee_1_nc), .enable(_00EE), .T1(T1),
    .H(H));
  _00E0 u_00e0_1 (.T1(T1), .enable(_00E0), .RE(RE), .EC(n00e0_1_ec), .NC(n00e0_1_nc));
  _1NNN u_1nnn_1 (
    .NNN(NNN), .PC(n1nnn_1_pc), .SPC(n1nnn_1_spc), .EC(n1nnn_1_ec), .T1(T1), .NC(n1nnn_1_nc), .enable(_1NNN),
    .H(H));
  _2NNN u_2nnn_1 (
    .nbrsaut(nbrsaut), .NNN(NNN), .PC(PC), .Snbrsaut(n2nnn_1_snbrsaut), .nbrsaut_2(n2nnn_1_nbrsaut_2),
    .PC_2(n2nnn_1_pc_2), .SPC(n2nnn_1_spc), .saut(saut_2), .Ssaut(Ssaut), .EC(n2nnn_1_ec), .T1(T1), .T2(T2),
    .NC(n2nnn_1_nc), .enable(_2NNN), .H(H));
  _6XKK u_6xkk_1 (
    .X(X), .KK(KK), .T1(T1), .enable(_6XKK), .AX(n6xkk_1_ax), .VX(n6xkk_1_vx), .SVX(n6xkk_1_svx),
    .EC(n6xkk_1_ec), .NC(n6xkk_1_nc), .H(H));
  _7XKK u_7xkk_1 (
    .X(X), .KK(KK), .VX(VX), .T1(T1), .enable(_7XKK), .AX(n7xkk_1_ax), .VX_2(n7xkk_1_vx_2),
    .SVX(n7xkk_1_svx), .EC(n7xkk_1_ec), .NC(n7xkk_1_nc), .H(H));
  assign or_1_out = n3xnn_1_pc_2 | n1nnn_1_pc | n4xkk_1_pc_2 | n2nnn_1_pc_2 | n5xy0_1_pc_2;  // OR_Gate or_1, 12 bits wide
  or or_2 (or_2_out, n3xnn_1_spc, n1nnn_1_spc, n4xkk_1_spc, n2nnn_1_spc, n5xy0_1_spc);
  or or_3 (EC, n3xnn_1_ec, n0nnn_1_ec, n00e0_1_ec, n1nnn_1_ec, n2nnn_1_ec, n4xkk_1_ec, n5xy0_1_ec, n6xkk_1_ec, n7xkk_1_ec, n00ee_1_ec);
  assign NC = n3xnn_1_nc | n0nnn_1_nc | n00e0_1_nc | n1nnn_1_nc | n2nnn_1_nc | n4xkk_1_nc | n5xy0_1_nc | n6xkk_1_nc | n7xkk_1_nc | n00ee_1_nc;  // OR_Gate or_4, 4 bits wide
  assign PC_2 = n00ee_1_pc | or_1_out;  // OR_Gate or_5, 12 bits wide
  or or_6 (SPC, n00ee_1_spc, or_2_out);
  assign AX = n3xnn_1_ax | n4xkk_1_ax | n5xy0_1_ax | n6xkk_1_ax | n7xkk_1_ax;  // OR_Gate or_7, 4 bits wide
  assign VX_2 = n6xkk_1_vx | n7xkk_1_vx_2;  // OR_Gate or_8, 8 bits wide
  or or_9 (SVX, n6xkk_1_svx, n7xkk_1_svx);
  or or_10 (Snbrsaut, n2nnn_1_snbrsaut, n00ee_1_snbrsaut);
  assign nbrsaut_2 = n00ee_1_nbrsaut_2 | n2nnn_1_nbrsaut_2;  // OR_Gate or_11, 4 bits wide
endmodule

module _0NNN (
  input  enable,
  output EC,
  output [3:0] NC
);

  wire [3:0] bit_extender_1_out;

  assign bit_extender_1_out = {{3{enable}}, enable};  // Bit_Extender bit_extender_1
  and and_1 (EC, 1'b1, enable);
  assign NC = 4'b0001 & bit_extender_1_out;  // AND_Gate and_2, 4 bits wide

  // Notes on the sheet:
  //   0NNN - [                     ] - "SYS addr"
  //   Calls RCA 1802 program at address NNN. Not necessary for most ROMs.
endmodule

module _00E0 (
  input  T1,
  input  enable,
  output RE,
  output EC,
  output [3:0] NC
);

  wire [3:0] bit_extender_1_out;

  and and_1 (RE, T1, enable);
  assign bit_extender_1_out = {{3{enable}}, enable};  // Bit_Extender bit_extender_1
  and and_2 (EC, 1'b1, enable);
  assign NC = 4'b0011 & bit_extender_1_out;  // AND_Gate and_3, 4 bits wide

  // Notes on the sheet:
  //   00E0 - [  disp_clear()       ] - CLS
  //   Clears the screen.
endmodule

module _00EE (
  input  [3:0] nbrsaut,
  input  [11:0] saut,
  input  H,
  input  T1,
  input  T2,
  input  enable,
  output Snbrsaut,
  output [3:0] nbrsaut_2,
  output [11:0] PC,
  output SPC,
  output EC,
  output [3:0] NC
);

  wire and_3_out, and_4_out, and_5_out, and_7_out, d_ff_1_q, not_1_out, not_2_out, subtractor_1_bout;
  wire [3:0] and_1_out, bit_extender_1_out, bit_extender_3_out, bit_extender_4_out, subtractor_1_out;
  wire [11:0] bit_extender_2_out;

  assign bit_extender_1_out = {{3{enable}}, enable};  // Bit_Extender bit_extender_1
  assign bit_extender_2_out = {{11{and_4_out}}, and_4_out};  // Bit_Extender bit_extender_2
  assign and_1_out = nbrsaut & bit_extender_1_out;  // AND_Gate and_1, 4 bits wide
  assign PC = saut & bit_extender_2_out;  // AND_Gate and_2, 12 bits wide
  Subtractor #(.width(4)) subtractor_1 (
    .a(and_1_out), .b(4'b0001), .out(subtractor_1_out), .bin(1'b0), .bout(subtractor_1_bout));
  not not_1 (not_1_out, subtractor_1_bout);
  and and_3 (and_3_out, enable, T1);
  and and_4 (and_4_out, T2, enable);
  assign bit_extender_3_out = {{3{not_1_out}}, not_1_out};  // Bit_Extender bit_extender_3
  and and_5 (and_5_out, and_3_out, enable);
  assign nbrsaut_2 = subtractor_1_out & bit_extender_3_out;  // AND_Gate and_6, 4 bits wide
  D_Flip_Flop d_ff_1 (
    .clk(and_5_out), .D(not_1_out), .Q(d_ff_1_q), .preset(1'b0), .en(enable), .reset(not_2_out));  // open: Qn
  not not_2 (not_2_out, enable);
  and and_7 (and_7_out, d_ff_1_q, and_4_out);
  assign bit_extender_4_out = {{3{enable}}, enable};  // Bit_Extender bit_extender_4
  SAVD savd_1 (.H(H), .T(and_3_out), .clear(not_2_out), .S(Snbrsaut));
  SAVD savd_2 (.H(H), .T(and_7_out), .clear(not_2_out), .S(SPC));
  and and_8 (EC, 1'b1, enable);
  assign NC = 4'b0100 & bit_extender_4_out;  // AND_Gate and_9, 4 bits wide

  // Notes on the sheet:
  //   00EE - [  return             ] - RET
  //   Returns from a subroutine.
endmodule

module _1NNN (
  input  [11:0] NNN,
  input  H,
  input  T1,
  input  enable,
  output [11:0] PC,
  output SPC,
  output EC,
  output [3:0] NC
);

  wire and_1_out, not_1_out;
  wire [3:0] bit_extender_2_out;
  wire [11:0] bit_extender_1_out;

  and and_1 (and_1_out, T1, enable);
  assign bit_extender_1_out = {{11{and_1_out}}, and_1_out};  // Bit_Extender bit_extender_1
  assign PC = NNN & bit_extender_1_out;  // AND_Gate and_2, 12 bits wide
  not not_1 (not_1_out, enable);
  assign bit_extender_2_out = {{3{enable}}, enable};  // Bit_Extender bit_extender_2
  SAVD savd_1 (.H(H), .T(and_1_out), .clear(not_1_out), .S(SPC));
  and and_3 (EC, 1'b1, enable);
  assign NC = 4'b0011 & bit_extender_2_out;  // AND_Gate and_4, 4 bits wide

  // Notes on the sheet:
  //   1nnn - [  goto NNN           ] - JP addr
  //   Jumps to address NNN.
endmodule

module _2NNN (
  input  [3:0] nbrsaut,
  input  [11:0] NNN,
  input  [11:0] PC,
  input  H,
  input  T1,
  input  T2,
  input  enable,
  output Snbrsaut,
  output [3:0] nbrsaut_2,
  output [11:0] PC_2,
  output SPC,
  output [11:0] saut,
  output Ssaut,
  output EC,
  output [3:0] NC
);

  wire adder_1_cout, and_3_out, and_4_out, not_2_out;
  wire [3:0] adder_1_out, and_5_out, and_6_out, and_7_out, and_8_out, bit_extender_3_out, bit_extender_4_out,
       bit_extender_5_out, bit_extender_6_out, not_1_out, or_1_out;
  wire [11:0] bit_extender_1_out, bit_extender_2_out;

  assign bit_extender_1_out = {{11{and_4_out}}, and_4_out};  // Bit_Extender bit_extender_1
  assign bit_extender_2_out = {{11{and_3_out}}, and_3_out};  // Bit_Extender bit_extender_2
  Adder #(.width(4)) adder_1 (.a(nbrsaut), .b(4'b0001), .out(adder_1_out), .cin(1'b0), .cout(adder_1_cout));
  assign PC_2 = NNN & bit_extender_1_out;  // AND_Gate and_1, 12 bits wide
  assign saut = PC & bit_extender_2_out;  // AND_Gate and_2, 12 bits wide
  and and_3 (and_3_out, enable, T1);
  and and_4 (and_4_out, T2, enable);
  assign not_1_out = ~bit_extender_3_out;  // NOT_Gate not_1, 4 bits wide
  assign bit_extender_3_out = {{3{adder_1_cout}}, adder_1_cout};  // Bit_Extender bit_extender_3
  assign and_5_out = adder_1_out & not_1_out;  // AND_Gate and_5, 4 bits wide
  assign and_6_out = bit_extender_3_out & nbrsaut;  // AND_Gate and_6, 4 bits wide
  assign or_1_out = and_5_out | and_6_out;  // OR_Gate or_1, 4 bits wide
  not not_2 (not_2_out, enable);
  assign bit_extender_4_out = {{3{enable}}, enable};  // Bit_Extender bit_extender_4
  SAVD savd_1 (.H(H), .T(and_4_out), .clear(not_2_out), .S(Snbrsaut));
  assign and_7_out = or_1_out & bit_extender_5_out;  // AND_Gate and_7, 4 bits wide
  assign bit_extender_5_out = {{3{and_4_out}}, and_4_out};  // Bit_Extender bit_extender_5
  assign and_8_out = nbrsaut & bit_extender_6_out;  // AND_Gate and_8, 4 bits wide
  assign bit_extender_6_out = {{3{and_3_out}}, and_3_out};  // Bit_Extender bit_extender_6
  SAVD savd_2 (.H(H), .T(and_4_out), .clear(not_2_out), .S(SPC));
  SAVD savd_3 (.H(H), .T(and_3_out), .clear(not_2_out), .S(Ssaut));
  and and_9 (EC, 1'b1, enable);
  assign NC = 4'b0100 & bit_extender_4_out;  // AND_Gate and_10, 4 bits wide
  assign nbrsaut_2 = and_7_out | and_8_out;  // OR_Gate or_2, 4 bits wide

  // Notes on the sheet:
  //   2nnn - [  *(0xNNN)()         ] - CALL addr
  //   Calls subroutine at NNN.
endmodule

module _3XNN (
  input  [3:0] X,
  input  [11:0] PC,
  input  [7:0] VX,
  input  [7:0] KK,
  input  H,
  input  T1,
  input  enable,
  output [3:0] AX,
  output [11:0] PC_2,
  output SPC,
  output EC,
  output [3:0] NC
);

  wire and_1_out, and_2_out, comparator_1_eq, not_1_out;
  wire [3:0] bit_extender_3_out, bit_extender_4_out;
  wire [8:0] bit_extender_1_out, bit_extender_2_out;
  wire [11:0] adder_1_out, bit_extender_5_out;

  Adder #(.width(12)) adder_1 (.a(PC), .b(12'h2), .out(adder_1_out), .cin(1'b0));  // open: cout
  assign bit_extender_1_out = {{1{1'b0}}, VX};  // Bit_Extender bit_extender_1
  assign bit_extender_2_out = {{1{1'b0}}, KK};  // Bit_Extender bit_extender_2
  and and_1 (and_1_out, T1, enable);
  Comparator #(.width(9)) comparator_1 (
    .a(bit_extender_1_out), .b(bit_extender_2_out), .eq(comparator_1_eq));  // open: gt, lt
  and and_2 (and_2_out, comparator_1_eq, and_1_out);
  not not_1 (not_1_out, enable);
  assign bit_extender_3_out = {{3{enable}}, enable};  // Bit_Extender bit_extender_3
  assign bit_extender_4_out = {{3{enable}}, enable};  // Bit_Extender bit_extender_4
  assign bit_extender_5_out = {{11{and_2_out}}, and_2_out};  // Bit_Extender bit_extender_5
  and and_3 (EC, 1'b1, enable);
  assign NC = 4'b0011 & bit_extender_3_out;  // AND_Gate and_4, 4 bits wide
  assign AX = X & bit_extender_4_out;  // AND_Gate and_5, 4 bits wide
  assign PC_2 = adder_1_out & bit_extender_5_out;  // AND_Gate and_6, 12 bits wide
  SAVD savd_1 (.H(H), .T(and_2_out), .clear(not_1_out), .S(SPC));

  // Notes on the sheet:
  //   3xkk - [  if(Vx==NN)         ] - SE Vx, byte
  //   Skips the next instruction if VX equals NN. (Usually the next instruction is a jump to skip a code block)
endmodule

module _4XKK (
  input  [3:0] X,
  input  [11:0] PC,
  input  [7:0] VX,
  input  [7:0] KK,
  input  H,
  input  T1,
  input  enable,
  output [3:0] AX,
  output [11:0] PC_2,
  output SPC,
  output EC,
  output [3:0] NC
);

  wire and_1_out, and_2_out, comparator_1_eq, not_1_out, not_2_out;
  wire [3:0] bit_extender_3_out, bit_extender_5_out;
  wire [8:0] bit_extender_1_out, bit_extender_2_out;
  wire [11:0] adder_1_out, bit_extender_4_out;

  assign bit_extender_1_out = {{1{1'b0}}, VX};  // Bit_Extender bit_extender_1
  assign bit_extender_2_out = {{1{1'b0}}, KK};  // Bit_Extender bit_extender_2
  Adder #(.width(12)) adder_1 (.a(PC), .b(12'h2), .out(adder_1_out), .cin(1'b0));  // open: cout
  Comparator #(.width(9)) comparator_1 (
    .a(bit_extender_1_out), .b(bit_extender_2_out), .eq(comparator_1_eq));  // open: gt, lt
  and and_1 (and_1_out, T1, enable);
  not not_1 (not_1_out, comparator_1_eq);
  and and_2 (and_2_out, not_1_out, and_1_out);
  not not_2 (not_2_out, enable);
  assign bit_extender_3_out = {{3{enable}}, enable};  // Bit_Extender bit_extender_3
  assign bit_extender_4_out = {{11{and_2_out}}, and_2_out};  // Bit_Extender bit_extender_4
  assign bit_extender_5_out = {{3{enable}}, enable};  // Bit_Extender bit_extender_5
  assign AX = X & bit_extender_3_out;  // AND_Gate and_3, 4 bits wide
  assign PC_2 = adder_1_out & bit_extender_4_out;  // AND_Gate and_4, 12 bits wide
  SAVD savd_1 (.H(H), .T(and_2_out), .clear(not_2_out), .S(SPC));
  and and_5 (EC, 1'b1, enable);
  assign NC = 4'b0011 & bit_extender_5_out;  // AND_Gate and_6, 4 bits wide

  // Notes on the sheet:
  //   4xkk - [  if(Vx!=NN)         ] - SNE Vx, byte
  //   Skips the next instruction if VX doesn't equal NN. (Usually the next instruction is a jump to skip a code block)
endmodule

module _5XY0 (
  input  [3:0] Y,
  input  [3:0] X,
  input  [11:0] PC,
  input  [7:0] VX,
  input  [7:0] VY,
  input  H,
  input  T1,
  input  enable,
  output [3:0] AY,
  output [3:0] AX,
  output [11:0] PC_2,
  output SPC,
  output EC,
  output [3:0] NC
);

  wire and_1_out, and_2_out, comparator_1_eq, not_1_out;
  wire [3:0] bit_extender_3_out, bit_extender_4_out, bit_extender_6_out;
  wire [8:0] bit_extender_1_out, bit_extender_2_out;
  wire [11:0] adder_1_out, bit_extender_5_out;

  Adder #(.width(12)) adder_1 (.a(PC), .b(12'h2), .out(adder_1_out), .cin(1'b0));  // open: cout
  assign bit_extender_1_out = {{1{1'b0}}, VX};  // Bit_Extender bit_extender_1
  assign bit_extender_2_out = {{1{1'b0}}, VY};  // Bit_Extender bit_extender_2
  and and_1 (and_1_out, T1, enable);
  Comparator #(.width(9)) comparator_1 (
    .a(bit_extender_1_out), .b(bit_extender_2_out), .eq(comparator_1_eq));  // open: gt, lt
  and and_2 (and_2_out, comparator_1_eq, and_1_out);
  not not_1 (not_1_out, enable);
  assign bit_extender_3_out = {{3{enable}}, enable};  // Bit_Extender bit_extender_3
  assign bit_extender_4_out = {{3{enable}}, enable};  // Bit_Extender bit_extender_4
  assign PC_2 = adder_1_out & bit_extender_5_out;  // AND_Gate and_3, 12 bits wide
  assign bit_extender_5_out = {{11{and_2_out}}, and_2_out};  // Bit_Extender bit_extender_5
  and and_4 (EC, 1'b1, enable);
  assign NC = 4'b0011 & bit_extender_6_out;  // AND_Gate and_5, 4 bits wide
  assign bit_extender_6_out = {{3{enable}}, enable};  // Bit_Extender bit_extender_6
  assign AY = Y & bit_extender_3_out;  // AND_Gate and_6, 4 bits wide
  assign AX = X & bit_extender_4_out;  // AND_Gate and_7, 4 bits wide
  SAVD savd_1 (.H(H), .T(and_2_out), .clear(not_1_out), .S(SPC));

  // Notes on the sheet:
  //   5xy0 - [  if(Vx==Vy)         ] - SE Vx, Vy
  //   Skips the next instruction if VX equals VY. (Usually the next instruction is a jump to skip a code block)
endmodule

module _6XKK (
  input  [3:0] X,
  input  [7:0] KK,
  input  H,
  input  T1,
  input  enable,
  output [3:0] AX,
  output [7:0] VX,
  output SVX,
  output EC,
  output [3:0] NC
);

  wire and_1_out, not_1_out;
  wire [3:0] bit_extender_2_out, bit_extender_3_out;
  wire [7:0] bit_extender_1_out;

  assign bit_extender_1_out = {{7{and_1_out}}, and_1_out};  // Bit_Extender bit_extender_1
  and and_1 (and_1_out, T1, enable);
  assign VX = KK & bit_extender_1_out;  // AND_Gate and_2, 8 bits wide
  not not_1 (not_1_out, enable);
  assign bit_extender_2_out = {{3{enable}}, enable};  // Bit_Extender bit_extender_2
  assign bit_extender_3_out = {{3{enable}}, enable};  // Bit_Extender bit_extender_3
  and and_3 (EC, 1'b1, enable);
  assign NC = 4'b0011 & bit_extender_2_out;  // AND_Gate and_4, 4 bits wide
  assign AX = X & bit_extender_3_out;  // AND_Gate and_5, 4 bits wide
  SAVD savd_1 (.H(H), .T(and_1_out), .clear(not_1_out), .S(SVX));

  // Notes on the sheet:
  //   6xkk - [  Vx = NN            ] - LD Vx, byte
  //   Sets VX to NN.
endmodule

module _7XKK (
  input  [3:0] X,
  input  [7:0] KK,
  input  [7:0] VX,
  input  H,
  input  T1,
  input  enable,
  output [3:0] AX,
  output [7:0] VX_2,
  output SVX,
  output EC,
  output [3:0] NC
);

  wire and_1_out, not_1_out;
  wire [3:0] bit_extender_5_out, bit_extender_6_out;
  wire [7:0] bit_extender_3_out, bit_extender_4_out;
  wire [8:0] adder_1_out, bit_extender_1_out, bit_extender_2_out;

  assign bit_extender_1_out = {{1{1'b0}}, KK};  // Bit_Extender bit_extender_1
  assign bit_extender_2_out = {{1{1'b0}}, VX};  // Bit_Extender bit_extender_2
  Adder #(.width(9)) adder_1 (
    .a(bit_extender_1_out), .b(bit_extender_2_out), .out(adder_1_out), .cin(1'b0));  // open: cout
  Bit_Extender #(.in_width(9), .out_width(8)) bit_extender_3 (.in(adder_1_out), .out(bit_extender_3_out));
  and and_1 (and_1_out, T1, enable);
  assign bit_extender_4_out = {{7{and_1_out}}, and_1_out};  // Bit_Extender bit_extender_4
  not not_1 (not_1_out, enable);
  assign bit_extender_5_out = {{3{enable}}, enable};  // Bit_Extender bit_extender_5
  assign VX_2 = bit_extender_3_out & bit_extender_4_out;  // AND_Gate and_2, 8 bits wide
  and and_3 (EC, 1'b1, enable);
  assign NC = 4'b0011 & bit_extender_6_out;  // AND_Gate and_4, 4 bits wide
  assign bit_extender_6_out = {{3{enable}}, enable};  // Bit_Extender bit_extender_6
  assign AX = X & bit_extender_5_out;  // AND_Gate and_5, 4 bits wide
  SAVD savd_1 (.H(H), .T(and_1_out), .clear(not_1_out), .S(SVX));

  // Notes on the sheet:
  //   7xkk - [  Vx += NN           ] - ADD Vx, byte
  //   Adds NN to VX. (Carry flag is not changed)
endmodule
