// Logisim project mini_chip8_aluG.circ as structural Verilog: 7 circuits, main circuit ALU_G
module ALU_G (
  input  [7:0] VX,
  input  [7:0] VY,
  input  [3:0] B1,
  input  [11:0] I,
  input  [7:0] DR,
  input  SCP,
  input  enable,
  input  H,
  output [5:0] SCX,
  output [4:0] SCY,
  output NC,
  output [11:0] AR,
  output SCstore,
  output SSCP,
  output C,
  output SVF,
  output [7:0] DF
);

  wire and_1_out, cylpix_1_end, not_1_out, not_2_out;
  wire [1:0] cylpix_1_v1;
  wire [3:0] caljk_1_j, caljk_1_k;

  not not_1 (not_1_out, enable);
  and and_1 (and_1_out, enable, not_2_out);
  CALXY calxy_1 (.VX(VX), .J(caljk_1_j), .VY(VY), .K(caljk_1_k), .SCX(SCX), .SCY(SCY));
  CALJK caljk_1 (
    .enable(enable), .H(H), .clear(not_1_out), .b1(B1), .K(caljk_1_k), .J(caljk_1_j), .\end (NC),
    .E1(cylpix_1_end));
  CALP calp_1 (
    .I(I), .K(caljk_1_k), .DR(DR), .enable(enable), .J(caljk_1_j), .SCP(SCP), .AR(AR), .SCstore(SCstore),
    .SSCP(SSCP), .CF(SVF), .DF(DF), .C(C), .SJ(cylpix_1_v1));
  CYLPIX cylpix_1 (.enable(and_1_out), .clear(not_1_out), .H(H), .V1(cylpix_1_v1), .\end (cylpix_1_end));
  not not_2 (not_2_out, NC);

  // Notes on the sheet:
  //   SCP: pull=down
  //   DR: pull=down
  //   B1: pull=down
  //   I: pull=down
  //   VX: pull=down
  //   VY: pull=down
  //   enable: pull=down
  //   H: pull=down
endmodule

module CALJK (
  input  E1,
  input  enable,
  input  H,
  input  clear,
  input  [3:0] b1,
  output [3:0] K,
  output [3:0] J,
  output \end 
);

  wire and_1_out, and_2_out, and_3_out, and_4_out, and_5_out, and_6_out, comparator_1_lt, comparator_2_eq,
       comparator_2_lt, d_ff_1_q, not_1_out, or_1_out, or_2_out;
  wire [3:0] bit_extender_1_out, bit_extender_2_out, counter_2_q;
  wire [4:0] bit_extender_3_out, bit_extender_4_out, counter_1_q;

  and and_1 (and_1_out, E1, enable);
  and and_2 (and_2_out, enable, comparator_1_lt);
  and and_3 (and_3_out, comparator_1_lt, or_1_out, H);
  and and_4 (and_4_out, comparator_1_lt, d_ff_1_q);
  and and_5 (and_5_out, not_1_out, and_1_out, and_4_out, comparator_2_lt);
  and and_6 (and_6_out, comparator_2_lt, and_4_out, H);
  Counter #(.width(5), .max('h1f)) counter_1 (
    .load(1'b0), .D({5{1'b0}}), .count(and_2_out), .Q(counter_1_q), .clk(and_3_out), .clr(clear));  // open: carry
  or or_1 (or_1_out, clear, comparator_2_eq);
  D_Flip_Flop #(.trigger("falling")) d_ff_1 (
    .clk(H), .D(1'b1), .Q(d_ff_1_q), .preset(1'b0), .en(and_1_out), .reset(or_2_out));  // open: Qn
  or or_2 (or_2_out, clear, comparator_2_eq);
  Counter #(.width(4), .max('hf)) counter_2 (
    .load(1'b0), .D(4'b0000), .count(and_5_out), .Q(counter_2_q), .clk(and_6_out), .clr(or_1_out));  // open: carry
  assign bit_extender_1_out = {{3{comparator_1_lt}}, comparator_1_lt};  // Bit_Extender bit_extender_1
  Bit_Extender #(.in_width(5), .out_width(4)) bit_extender_2 (.in(counter_1_q), .out(bit_extender_2_out));
  assign K = bit_extender_1_out & bit_extender_2_out;  // AND_Gate and_7, 4 bits wide
  assign J = bit_extender_1_out & counter_2_q;  // AND_Gate and_8, 4 bits wide
  Comparator #(.width(5)) comparator_1 (
    .a(counter_1_q), .b(bit_extender_3_out), .eq(\end ), .lt(comparator_1_lt));  // open: gt
  assign bit_extender_3_out = {{1{1'b0}}, b1};  // Bit_Extender bit_extender_3
  not not_1 (not_1_out, \end );
  assign bit_extender_4_out = {{1{1'b0}}, counter_2_q};  // Bit_Extender bit_extender_4
  Comparator #(.width(5)) comparator_2 (
    .a(bit_extender_4_out), .b(5'b01000), .eq(comparator_2_eq), .lt(comparator_2_lt));  // open: gt

  // Notes on the sheet:
  //   b1: pull=down
  //   enable: pull=down
  //   clear: pull=down
  //   E1: pull=down
  //   H: pull=down
endmodule

module CALXY (
  input  [7:0] VX,
  input  [3:0] J,
  input  [7:0] VY,
  input  [3:0] K,
  output [5:0] SCX,
  output [4:0] SCY
);

  wire [7:0] adder_1_out, adder_2_out, bit_extender_1_out, bit_extender_2_out;
  wire [8:0] bit_extender_3_out, bit_extender_4_out, divider_1_rem, divider_2_rem;

  assign bit_extender_1_out = {{4{1'b0}}, J};  // Bit_Extender bit_extender_1
  assign bit_extender_2_out = {{4{1'b0}}, K};  // Bit_Extender bit_extender_2
  Adder adder_1 (.a(VX), .b(bit_extender_1_out), .out(adder_1_out), .cin(1'b0));  // open: cout
  Adder adder_2 (.a(VY), .b(bit_extender_2_out), .out(adder_2_out), .cin(1'b0));  // open: cout
  assign bit_extender_3_out = {{1{1'b0}}, adder_1_out};  // Bit_Extender bit_extender_3
  assign bit_extender_4_out = {{1{1'b0}}, adder_2_out};  // Bit_Extender bit_extender_4
  Divider #(.width(9)) divider_1 (
    .a(bit_extender_3_out), .b(9'h40), .upper({9{1'b0}}), .rem(divider_1_rem));  // open: out
  // Probe on 9'h40
  Divider #(.width(9)) divider_2 (
    .a(bit_extender_4_out), .b(9'h20), .upper({9{1'b0}}), .rem(divider_2_rem));  // open: out
  // Probe on 9'h20
  Bit_Extender #(.in_width(9), .out_width(6)) bit_extender_5 (.in(divider_1_rem), .out(SCX));
  Bit_Extender #(.in_width(9), .out_width(5)) bit_extender_6 (.in(divider_2_rem), .out(SCY));

  // Notes on the sheet:
  //   VX: pull=down
  //   VY: pull=down
  //   K: pull=down
  //   J: pull=down
endmodule

module CALP (
  input  [11:0] I,
  input  [3:0] K,
  input  [7:0] DR,
  input  enable,
  input  [3:0] J,
  input  [1:0] SJ,
  input  SCP,
  output [11:0] AR,
  output SCstore,
  output SSCP,
  output C,
  output CF,
  output [7:0] DF
);

  wire adder_2_cout, adder_2_out, and_1_out, and_2_out, and_5_out, d_ff_1_qn, not_1_out, recpix_1_out_4,
       recpix_1_out_5;
  wire [11:0] bit_extender_1_out;

  and and_1 (and_1_out, enable, recpix_1_out_4);
  RECPIX recpix_1 (.SJ(SJ), .Enable(enable), .out_5(recpix_1_out_5), .out_4(recpix_1_out_4), .SCP(SCP));
  assign bit_extender_1_out = {{8{1'b0}}, K};  // Bit_Extender bit_extender_1
  not not_1 (not_1_out, enable);
  Adder #(.width(12)) adder_1 (.a(I), .b(bit_extender_1_out), .out(AR), .cin(1'b0));  // open: cout
  INIMRP inimrp_1 (.DR(DR), .enable(and_1_out), .J(J), .S(SCstore));
  Adder #(.width(1)) adder_2 (.a(SCstore), .b(recpix_1_out_5), .out(adder_2_out), .cin(1'b0), .cout(adder_2_cout));
  D_Flip_Flop d_ff_1 (
    .clk(and_2_out), .D(d_ff_1_qn), .Q(CF), .Qn(d_ff_1_qn), .preset(1'b0), .en(enable), .reset(not_1_out));
  and and_2 (and_2_out, C, d_ff_1_qn);
  and and_3 (SSCP, SCstore, adder_2_out);
  and and_4 (C, SCstore, adder_2_cout);
  and and_5 (and_5_out, CF, enable);
  assign DF = {{7{1'b0}}, and_5_out};  // Bit_Extender bit_extender_2

  // Notes on the sheet:
  //   SCP: pull=down
  //   I: pull=down
  //   K: pull=down
  //   enable: pull=down
  //   DR: pull=down
  //   SJ: pull=down
  //   J: pull=down
endmodule

module RECPIX (
  input  [1:0] SJ,
  input  Enable,
  input  SCP,
  output out_4,
  output out_5
);

  wire and_2_out, and_3_out, and_4_out, and_5_out, not_1_out, not_2_out, not_3_out, not_4_out, or_1_out;
  wire [1:0] and_1_out, bit_extender_1_out;

  assign and_1_out = SJ & bit_extender_1_out;  // AND_Gate and_1, 2 bits wide
  assign bit_extender_1_out = {{1{Enable}}, Enable};  // Bit_Extender bit_extender_1
  not not_1 (not_1_out, and_1_out[1]);
  not not_2 (not_2_out, and_1_out[0]);
  not not_3 (not_3_out, Enable);
  and and_2 (and_2_out, and_1_out[0], not_1_out);
  or or_1 (or_1_out, and_2_out, not_3_out);
  and and_3 (and_3_out, not_2_out, and_1_out[1]);
  and and_4 (and_4_out, and_1_out[0], and_1_out[1]);
  not not_4 (not_4_out, or_1_out);
  or or_2 (out_4, and_4_out, and_5_out);
  and and_5 (and_5_out, not_4_out, out_4);
  D_Flip_Flop d_ff_1 (.clk(and_3_out), .D(SCP), .Q(out_5), .preset(1'b0), .en(Enable), .reset(or_1_out));  // open: Qn

  // Notes on the sheet:
  //   Enable: pull=down
  //   SCP: pull=down
  //   SJ: pull=down
endmodule

module CYLPIX (
  input  enable,
  input  clear,
  input  H,
  output [1:0] V1,
  output \end 
);

  wire and_1_out, or_1_out;
  wire [1:0] and_3_out, and_4_out, bit_extender_1_out, not_1_out;
  wire [3:0] counter_1_q;

  or or_1 (or_1_out, clear, and_1_out);
  Counter #(.width(4), .max('hf)) counter_1 (
    .load(1'b0), .D(4'b0000), .count(enable), .Q(counter_1_q), .clk(H), .clr(or_1_out));  // open: carry
  and and_1 (and_1_out, counter_1_q[1], counter_1_q[2]);
  assign bit_extender_1_out = {{1{counter_1_q[2]}}, counter_1_q[2]};  // Bit_Extender bit_extender_1
  assign not_1_out = ~bit_extender_1_out;  // NOT_Gate not_1, 2 bits wide
  and and_2 (\end , counter_1_q[2], counter_1_q[0]);
  assign and_3_out = 2'b01 & bit_extender_1_out;  // AND_Gate and_3, 2 bits wide
  assign V1 = and_3_out | and_4_out;  // OR_Gate or_2, 2 bits wide
  assign and_4_out = not_1_out & counter_1_q[1:0];  // AND_Gate and_4, 2 bits wide
endmodule

module INIMRP (
  input  [7:0] DR,
  input  enable,
  input  [3:0] J,
  output S
);

  wire and_1_out, and_2_out, and_3_out, and_4_out, and_5_out, and_6_out, and_7_out, and_8_out,
       decoder_1_out0, decoder_1_out1, decoder_1_out2, decoder_1_out3, decoder_1_out4, decoder_1_out5,
       decoder_1_out6, decoder_1_out7;
  wire [2:0] bit_extender_1_out;

  Decoder #(.select(3)) decoder_1 (
    .out0(decoder_1_out0), .out1(decoder_1_out1), .out2(decoder_1_out2), .out3(decoder_1_out3),
    .out4(decoder_1_out4), .out5(decoder_1_out5), .out6(decoder_1_out6), .out7(decoder_1_out7),
    .sel(bit_extender_1_out), .en(enable));
  Pull_Resistor pull_resistor_1 (.node(decoder_1_out0));
  Pull_Resistor pull_resistor_2 (.node(decoder_1_out2));
  Pull_Resistor pull_resistor_3 (.node(decoder_1_out1));
  Pull_Resistor pull_resistor_4 (.node(decoder_1_out3));
  Bit_Extender #(.in_width(4), .out_width(3)) bit_extender_1 (.in(J), .out(bit_extender_1_out));
  Pull_Resistor pull_resistor_5 (.node(decoder_1_out7));
  Pull_Resistor pull_resistor_6 (.node(decoder_1_out5));
  Pull_Resistor pull_resistor_7 (.node(decoder_1_out6));
  Pull_Resistor pull_resistor_8 (.node(decoder_1_out4));
  and and_1 (and_1_out, DR[0], decoder_1_out7);
  and and_2 (and_2_out, DR[1], decoder_1_out6);
  and and_3 (and_3_out, DR[2], decoder_1_out5);
  and and_4 (and_4_out, DR[3], decoder_1_out4);
  and and_5 (and_5_out, DR[4], decoder_1_out3);
  and and_6 (and_6_out, DR[5], decoder_1_out2);
  and and_7 (and_7_out, DR[6], decoder_1_out1);
  and and_8 (and_8_out, DR[7], decoder_1_out0);
  or or_1 (S, and_1_out, and_2_out, and_3_out, and_4_out, and_5_out, and_6_out, and_7_out, and_8_out);

  // Notes on the sheet:
  //   J: pull=down
  //   DR: pull=down
  //   enable: pull=down
endmodule
