// Logisim project mini_chip8_aluH.circ as structural Verilog: 8 circuits, main circuit aluHexDec
module aluHexDec (
  input  [7:0] VX,
  input  [11:0] I,
  input  enable,
  input  H,
  output [7:0] DR,
  output [11:0] AR,
  output SR,
  output out_8
);

  wire savram_1_sel_hundred, savram_1_sel_ten, savram_1_sel_unit, tmphex_1_save;
  wire [1:0] tmphex_1_sel;
  wire [7:0] and_1_out, and_2_out, and_3_out, bit_extender_1_out, bit_extender_2_out, bit_extender_3_out,
       hexadec_1_output_hundred, hexadec_1_output_ten, hexadec_1_output_unit;

  tmpHex tmphex_1 (.enable(enable), .H(H), .save(tmphex_1_save), .Sel(tmphex_1_sel), .\end (out_8));
  hexadec hexadec_1 (
    .VX(VX), .Output_hundred(hexadec_1_output_hundred), .Output_unit(hexadec_1_output_unit),
    .Output_ten(hexadec_1_output_ten));
  savRam savram_1 (
    .I(I), .enable(enable), .Sel(tmphex_1_sel), .AR(AR), .Sel_unit(savram_1_sel_unit),
    .Sel_ten(savram_1_sel_ten), .Sel_hundred(savram_1_sel_hundred));
  assign bit_extender_1_out = {{7{savram_1_sel_hundred}}, savram_1_sel_hundred};  // Bit_Extender bit_extender_1
  assign bit_extender_2_out = {{7{savram_1_sel_ten}}, savram_1_sel_ten};  // Bit_Extender bit_extender_2
  assign bit_extender_3_out = {{7{savram_1_sel_unit}}, savram_1_sel_unit};  // Bit_Extender bit_extender_3
  or or_1 (SR, savram_1_sel_hundred, savram_1_sel_ten, savram_1_sel_unit, tmphex_1_save);
  assign and_1_out = hexadec_1_output_hundred & bit_extender_1_out;  // AND_Gate and_1, 8 bits wide
  assign and_2_out = hexadec_1_output_ten & bit_extender_2_out;  // AND_Gate and_2, 8 bits wide
  assign and_3_out = hexadec_1_output_unit & bit_extender_3_out;  // AND_Gate and_3, 8 bits wide
  assign DR = and_1_out | and_2_out | and_3_out;  // OR_Gate or_2, 8 bits wide
endmodule

module recuDiv (
  input  [7:0] VX,
  input  [7:0] DIV,
  output [7:0] S
);

  wire [7:0] divider_1_rem, subtractor_1_out;

  Divider divider_1 (.a(VX), .b(DIV), .upper({8{1'b0}}), .rem(divider_1_rem));  // open: out
  Subtractor subtractor_1 (.a(VX), .b(divider_1_rem), .out(subtractor_1_out), .bin(1'b0));  // open: bout
  Divider divider_2 (.a(subtractor_1_out), .b(DIV), .out(S), .upper({8{1'b0}}));  // open: rem
endmodule

module deci_hundred (
  input  [7:0] VX,
  output [7:0] S
);

  // Probe on 8'h64
  recuDiv recudiv_1 (.VX(VX), .DIV(8'h64), .S(S));
endmodule

module deci_ten (
  input  [7:0] VX,
  output [7:0] S
);

  wire [7:0] recudiv_1_s;

  // Probe on 8'ha
  recuDiv recudiv_1 (.VX(VX), .DIV(8'ha), .S(recudiv_1_s));
  Divider divider_1 (.a(recudiv_1_s), .b(8'ha), .upper({8{1'b0}}), .rem(S));  // open: out
endmodule

module deci_unit (
  input  [7:0] VX,
  input  [7:0] hundred,
  input  [7:0] ten,
  output [7:0] O
);

  wire [7:0] multiplier_1_out, multiplier_2_out, subtractor_1_out;

  // Probe on 8'h64
  // Probe on 8'ha
  Multiplier multiplier_1 (.a(hundred), .b(8'h64), .out(multiplier_1_out), .cin({8{1'b0}}));  // open: cout
  Multiplier multiplier_2 (.a(8'ha), .b(ten), .out(multiplier_2_out), .cin({8{1'b0}}));  // open: cout
  Subtractor subtractor_1 (.a(VX), .b(multiplier_1_out), .out(subtractor_1_out), .bin(1'b0));  // open: bout
  Subtractor subtractor_2 (.a(subtractor_1_out), .b(multiplier_2_out), .out(O), .bin(1'b0));  // open: bout
endmodule

module hexadec (
  input  [7:0] VX,
  output [7:0] Output_hundred,
  output [7:0] Output_unit,
  output [7:0] Output_ten
);

  deci_hundred deci_hundred_1 (.VX(VX), .S(Output_hundred));
  deci_ten deci_ten_1 (.VX(VX), .S(Output_ten));
  deci_unit deci_unit_1 (.VX(VX), .hundred(Output_hundred), .ten(Output_ten), .O(Output_unit));
endmodule

module savRam (
  input  [11:0] I,
  input  enable,
  input  [1:0] Sel,
  output [11:0] AR,
  output Sel_unit,
  output Sel_ten,
  output Sel_hundred
);

  wire [11:0] adder_1_out, adder_2_out, and_1_out, and_2_out, and_3_out, bit_extender_1_out,
       bit_extender_2_out, bit_extender_3_out;

  Adder #(.width(12)) adder_1 (.a(12'h1), .b(I), .out(adder_1_out), .cin(1'b0));  // open: cout
  Decoder #(.select(2), .disabled(0)) decoder_1 (
    .out0(Sel_hundred), .out1(Sel_ten), .out2(Sel_unit), .sel(Sel), .en(enable));  // open: out3
  Adder #(.width(12)) adder_2 (.a(adder_1_out), .b(12'h1), .out(adder_2_out), .cin(1'b0));  // open: cout
  assign and_1_out = I & bit_extender_1_out;  // AND_Gate and_1, 12 bits wide
  assign bit_extender_1_out = {{11{Sel_hundred}}, Sel_hundred};  // Bit_Extender bit_extender_1
  assign and_2_out = adder_1_out & bit_extender_2_out;  // AND_Gate and_2, 12 bits wide
  assign bit_extender_2_out = {{11{Sel_ten}}, Sel_ten};  // Bit_Extender bit_extender_2
  assign and_3_out = adder_2_out & bit_extender_3_out;  // AND_Gate and_3, 12 bits wide
  assign bit_extender_3_out = {{11{Sel_unit}}, Sel_unit};  // Bit_Extender bit_extender_3
  assign AR = and_1_out | and_2_out | and_3_out;  // OR_Gate or_1, 12 bits wide
endmodule

module tmpHex (
  input  enable,
  input  H,
  output save,
  output [1:0] Sel,
  output \end 
);

  wire and_1_out, and_2_out, comparator_1_eq, comparator_1_gt, comparator_1_lt, not_1_out;
  wire [7:0] counter_1_q;

  and and_1 (and_1_out, enable, comparator_1_lt);
  not not_1 (not_1_out, enable);
  Counter counter_1 (
    .load(1'b0), .D({8{1'b0}}), .count(and_1_out), .Q(counter_1_q), .clk(and_2_out), .clr(not_1_out));  // open: carry
  and and_2 (and_2_out, H, comparator_1_lt);
  Comparator #(.width(6)) comparator_1 (
    .a(counter_1_q[7:2]), .b(6'b000011), .gt(comparator_1_gt), .eq(comparator_1_eq), .lt(comparator_1_lt));
  or or_1 (save, counter_1_q[0], counter_1_q[1]);
  Bit_Extender #(.in_width(6), .out_width(2)) bit_extender_1 (.in(counter_1_q[7:2]), .out(Sel));
  or or_2 (\end , comparator_1_gt, comparator_1_eq);
endmodule
