// Logisim project mini_chip8_game.circ as structural Verilog: 9 circuits, main circuit GAMES
module GAMES (
  input  [11:0] Game_Adress,
  input  Game_Select,
  input  Select,
  output [7:0] Game_Data,
  output [11:0] Game_Size,
  output [7:0] Choice
);

  wire comparator_1_eq, demultiplexer_2_out0, demultiplexer_2_out1, demultiplexer_2_out2,
       demultiplexer_2_out3, demultiplexer_2_out4, demultiplexer_2_out5, demultiplexer_2_out6,
       demultiplexer_2_out7;
  wire [2:0] bit_extender_1_out;
  wire [3:0] counter_1_q;
  wire [7:0] bc_test_1_data, bcd_1_data, breakout_1_data, c8pic_1_data, maze_1_data, pong_1_data,
       voiture_1_data, x_mirror_1_data;
  wire [11:0] bc_test_1_size, bcd_1_size, breakout_1_size, c8pic_1_size, demultiplexer_1_out0,
       demultiplexer_1_out1, demultiplexer_1_out2, demultiplexer_1_out3, demultiplexer_1_out4,
       demultiplexer_1_out5, demultiplexer_1_out6, demultiplexer_1_out7, maze_1_size, pong_1_size,
       voiture_1_size, x_mirror_1_size;

  C8PIC c8pic_1 (
    .Address(demultiplexer_1_out0), .Select(demultiplexer_2_out0), .Data(c8pic_1_data), .Size(c8pic_1_size));
  bc_test bc_test_1 (
    .Address(demultiplexer_1_out1), .Data(bc_test_1_data), .Select(demultiplexer_2_out1),
    .Size(bc_test_1_size));
  MAZE maze_1 (.Address(demultiplexer_1_out2), .Data(maze_1_data), .Select(demultiplexer_2_out2), .Size(maze_1_size));
  BCD bcd_1 (.Address(demultiplexer_1_out3), .Data(bcd_1_data), .Select(demultiplexer_2_out3), .Size(bcd_1_size));
  X_MIRROR x_mirror_1 (
    .Address(demultiplexer_1_out4), .Data(x_mirror_1_data), .Select(demultiplexer_2_out4),
    .Size(x_mirror_1_size));
  Pong pong_1 (.Address(demultiplexer_1_out5), .Data(pong_1_data), .Select(demultiplexer_2_out5), .Size(pong_1_size));
  BREAKOUT breakout_1 (
    .Address(demultiplexer_1_out6), .Data(breakout_1_data), .Select(demultiplexer_2_out6),
    .Size(breakout_1_size));
  voiture voiture_1 (
    .Address(demultiplexer_1_out7), .Data(voiture_1_data), .Select(demultiplexer_2_out7),
    .Size(voiture_1_size));
  Counter #(.width(4), .max('hf)) counter_1 (
    .load(1'b0), .D(4'b0000), .count(1'b1), .Q(counter_1_q), .clk(Select), .clr(comparator_1_eq));  // open: carry
  Bit_Extender #(.in_width(4), .out_width(3)) bit_extender_1 (.in(counter_1_q), .out(bit_extender_1_out));
  Comparator #(.width(4)) comparator_1 (.a(counter_1_q), .b(4'b1000), .eq(comparator_1_eq));  // open: gt, lt
  Demultiplexer #(.select(3), .width(12), .disabled(0), .enable("false")) demultiplexer_1 (
    .out0(demultiplexer_1_out0), .out1(demultiplexer_1_out1), .out2(demultiplexer_1_out2),
    .out3(demultiplexer_1_out3), .out4(demultiplexer_1_out4), .out5(demultiplexer_1_out5),
    .out6(demultiplexer_1_out6), .out7(demultiplexer_1_out7), .in(Game_Adress), .sel(bit_extender_1_out));
  Demultiplexer #(.select(3), .disabled(0), .enable("false")) demultiplexer_2 (
    .out0(demultiplexer_2_out0), .out1(demultiplexer_2_out1), .out2(demultiplexer_2_out2),
    .out3(demultiplexer_2_out3), .out4(demultiplexer_2_out4), .out5(demultiplexer_2_out5),
    .out6(demultiplexer_2_out6), .out7(demultiplexer_2_out7), .in(Game_Select), .sel(bit_extender_1_out));
  Multiplexer #(.select(3), .width(8), .disabled(0), .enable("false")) multiplexer_1 (
    .in0(c8pic_1_data), .in1(bc_test_1_data), .in2(maze_1_data), .in3(bcd_1_data), .in4(x_mirror_1_data),
    .in5(pong_1_data), .in6(breakout_1_data), .in7(voiture_1_data), .out(Game_Data), .sel(bit_extender_1_out));
  Multiplexer #(.select(3), .width(12), .disabled(0), .enable("false")) multiplexer_2 (
    .in0(c8pic_1_size), .in1(bc_test_1_size), .in2(maze_1_size), .in3(bcd_1_size), .in4(x_mirror_1_size),
    .in5(pong_1_size), .in6(breakout_1_size), .in7(voiture_1_size), .out(Game_Size), .sel(bit_extender_1_out));
  Decoder #(.select(3), .enable("false")) decoder_1 (
    .out0(Choice[0]), .out1(Choice[1]), .out2(Choice[2]), .out3(Choice[3]), .out4(Choice[4]),
    .out5(Choice[5]), .out6(Choice[6]), .out7(Choice[7]), .sel(bit_extender_1_out));
endmodule

module C8PIC (
  input  [11:0] Address,
  input  Select,
  output [7:0] Data,
  output [11:0] Size
);

  ROM #(.addrWidth(12)) rom_1 (.addr(Address), .data(Data), .sel(Select));

  assign Size = 12'hb8;

  // Notes on the sheet:
  //   contents of rom_1 (hex, n*v repeats v):
  //   0 e0 a2 48 60 0 61 1e 62 0 d2 2 d2 12 72 8 32 40 12 a 60 0 61 3e 62 2 a2 4a d0 2e d1 2e 72 e d0 2e
  //   d1 2e a2 58 60 b 61 8 d0 1f 70 a a2 67 d0 1f 70 a a2 76 d0 1f 70 3 a2 85 d0 1f 70 a a2 94 d0 1f 12
  //   46 ff ff 14*c0 ff 13*80 ff 7*81 ff 7*81 15*80 ff 6*81 ff 7*80 ff 6*81 ff 6*81 ff ff
endmodule

module MAZE (
  input  [11:0] Address,
  input  Select,
  output [7:0] Data,
  output [11:0] Size
);

  ROM #(.addrWidth(12)) rom_1 (.addr(Address), .data(Data), .sel(Select));

  assign Size = 12'h3a;

  // Notes on the sheet:
  //   contents of rom_1 (hex, n*v repeats v):
  //   60 0 61 0 a2 22 c2 1 32 1 a2 1e d0 14 70 4 30 40 12 4 60 0 71 4 31 20 12 4 12 1c 80 40 20 10 20 40
  //   80 10
endmodule

module X_MIRROR (
  input  [11:0] Address,
  input  Select,
  output [7:0] Data,
  output [11:0] Size
);

  ROM #(.addrWidth(12)) rom_1 (.addr(Address), .data(Data), .sel(Select));

  assign Size = 12'h7e;

  // Notes on the sheet:
  //   contents of rom_1 (hex, n*v repeats v):
  //   66 1e 67 f 68 1f 69 f 6a 1e 6b 10 6c 1f 6d 10 a2 68 22 2e 60 2 e0 a1 22 44 60 8 e0 a1 22 38 60 4 e0
  //   a1 22 50 60 6 e0 a1 22 5c 12 14 d6 71 d8 91 da b1 dc d1 0 ee 77 ff 79 ff 7b 1 7d 1 22 2e 0 ee 77 1
  //   79 1 7b ff 7d ff 22 2e 0 ee 76 ff 78 1 7a ff 7c 1 22 2e 0 ee 76 1 78 ff 7a 1 7c ff 22 2e 0 ee 80
endmodule

module voiture (
  input  [11:0] Address,
  input  Select,
  output [7:0] Data,
  output [11:0] Size
);

  ROM #(.addrWidth(12)) rom_1 (.addr(Address), .data(Data), .sel(Select));

  assign Size = 12'h8c;

  // Notes on the sheet:
  //   contents of rom_1 (hex, n*v repeats v):
  //   0 e0 6a 4 6b 6 69 1 61 11 62 2 63 3c a2 73 d2 13 d3 13 61 14 62 0 a2 72 d2 11 72 8 32 40 12 1a 6d 7
  //   6e b 22 4e eb 9e 12 2e 12 34 ea 9e 12 28 12 40 22 4e 7d 1 22 4e 4f 1 12 40 12 28 22 4e 8d 95 22 4e
  //   48 1 12 34 12 28 12 4c a2 60 dd e9 88 f0 8c d0 7c 8 a2 69 dc e9 0 ee f ff 7 8 8 70 80 98 ff 3c 18 80
  //   40 20 1c 2 19 ff 3c 18 ff 80 80 80
endmodule

module Pong (
  input  [11:0] Address,
  input  Select,
  output [7:0] Data,
  output [11:0] Size
);

  ROM #(.addrWidth(12)) rom_1 (.addr(Address), .data(Data), .sel(Select));

  assign Size = 12'h10a;

  // Notes on the sheet:
  //   contents of rom_1 (hex, n*v repeats v):
  //   6a 2 6b c 6c 3f 6d c a2 ea da b6 dc d6 6e 0 22 d4 66 3 68 2 60 60 f0 15 f0 7 30 0 12 1a c7 17 77 8
  //   69 ff a2 f0 d6 71 a2 ea da b6 dc d6 60 1 e0 a1 7b fe 60 4 e0 a1 7b 2 60 1f 8b 2 da b6 8d 70 c0 a 7d
  //   fe 40 0 7d 2 60 0 60 1f 8d 2 dc d6 a2 f0 d6 71 86 84 87 94 60 3f 86 2 61 1f 87 12 46 2 12 78 46 3f
  //   12 82 47 1f 69 ff 47 0 69 1 d6 71 12 2a 68 2 63 1 80 70 80 b5 12 8a 68 fe 63 a 80 70 80 d5 3f 1 12
  //   a2 61 2 80 15 3f 1 12 ba 80 15 3f 1 12 c8 80 15 3f 1 12 c2 60 20 f0 18 22 d4 8e 34 22 d4 66 3e 33 1
  //   66 3 68 fe 33 1 68 2 12 16 79 ff 49 fe 69 ff 12 c8 79 1 49 2 69 1 60 4 f0 18 76 1 46 40 76 fe 12 6c
  //   a2 f2 fe 33 f2 65 f1 29 64 14 65 0 d4 55 74 15 f2 29 d4 55 0 ee 7*80
endmodule

module BREAKOUT (
  input  [11:0] Address,
  input  Select,
  output [7:0] Data,
  output [11:0] Size
);

  ROM #(.addrWidth(12)) rom_1 (.addr(Address), .data(Data), .sel(Select));

  assign Size = 12'h12c;

  // Notes on the sheet:
  //   contents of rom_1 (hex, n*v repeats v):
  //   6e 5 65 0 6b 6 6a 0 a3 c da b1 7a 4 3a 40 12 8 7b 2 3b 12 12 6 6c 20 6d 1f a3 10 dc d1 22 f6 60 0 61
  //   0 a3 12 d0 11 70 8 a3 e d0 11 60 40 f0 15 f0 7 30 0 12 34 c6 f 67 1e 68 1 69 ff a3 e d6 71 a3 10 dc
  //   d1 60 4 e0 a1 7c fe 60 6 e0 a1 7c 2 60 3f 8c 2 dc d1 a3 e d6 71 86 84 87 94 60 3f 86 2 61 1f 87 12
  //   47 1f 12 ac 46 0 68 1 46 3f 68 ff 47 0 69 1 d6 71 3f 1 12 aa 47 1f 12 aa 60 5 80 75 3f 0 12 aa 60 1
  //   f0 18 80 60 61 fc 80 12 a3 c d0 71 60 fe 89 3 22 f6 75 1 22 f6 45 60 12 de 12 46 69 ff 80 60 80 c5
  //   3f 1 12 ca 61 2 80 15 3f 1 12 e0 80 15 3f 1 12 ee 80 15 3f 1 12 e8 60 20 f0 18 a3 e 7e ff 80 e0 80 4
  //   61 0 d0 11 3e 0 12 30 12 de 78 ff 48 fe 68 ff 12 ee 78 1 48 2 68 1 60 4 f0 18 69 ff 12 70 a3 14 f5
  //   33 f2 65 f1 29 63 37 64 0 d3 45 73 5 f2 29 d3 45 0 ee f0 0 80 0 fc 0 aa
endmodule

module bc_test (
  input  [11:0] Address,
  input  Select,
  output [7:0] Data,
  output [11:0] Size
);

  ROM #(.addrWidth(12)) rom_1 (.addr(Address), .data(Data), .sel(Select));

  assign Size = 12'h2cc;

  // Notes on the sheet:
  //   contents of rom_1 (hex, n*v repeats v):
  //   0 e0 63 0 64 1 65 ee 35 ee 13 10 63 0 64 2 65 ee 66 ee 55 60 13 10 63 0 64 3 65 ee 45 fd 13 10 63 0
  //   64 4 65 ee 75 1 35 ef 13 10 63 0 64 5 6f 1 65 ee 66 ef 85 65 3f 0 13 10 63 0 64 6 6f 0 65 ef 66 ee
  //   85 65 3f 1 13 10 6f 0 63 0 64 7 65 ee 66 ef 85 67 3f 1 13 10 63 0 64 8 6f 1 65 ef 66 ee 85 67 3f 0
  //   13 10 63 0 64 9 65 f0 66 f 85 61 35 ff 13 10 63 1 64 0 65 f0 66 f 85 62 35 0 13 10 63 1 64 1 65 f0
  //   66 f 85 63 35 ff 13 10 6f 0 63 1 64 2 65 81 85 e 3f 1 13 10 63 1 64 3 6f 1 65 47 85 e 3f 0 13 10 63
  //   1 64 4 6f 0 65 1 85 6 3f 1 13 10 63 1 64 5 6f 1 65 2 85 6 3f 0 13 10 63 1 64 6 60 15 61 78 a3 d0 f1
  //   55 f1 65 30 15 13 10 31 78 13 10 63 1 64 7 60 8a a3 d0 f0 33 a3 d0 f0 65 30 1 13 10 60 1 f0 1e f0 65
  //   30 3 13 10 60 1 f0 1e f0 65 30 8 13 10 13 32 13 e a3 2a 60 13 61 9 d0 18 f3 29 60 22 61 b d0 15 f4
  //   29 60 28 61 b d0 15 13 e ff f0 f0 ff f0 f0 f0 ff a3 58 60 15 61 b 63 8 d0 18 70 8 f3 1e 30 2d 13 3a
  //   a3 70 60 2 61 18 63 8 d0 18 70 5 f3 1e 30 3e 13 4c 13 e f0 88 88 f0 88 88 88 f0 78 6*84 78 84 c4 a4
  //   94 8c 84 84 84 c0 a0 a0 c0 a0 a0 c0 0 0 0 a0 a0 e0 20 20 e0 8*0 c0 a0 a0 c0 a0 a0 c0 0 0 0 60 a0 c0
  //   80 60 0 0 0 60 80 40 20 c0 0 80 80 c0 80 80 80 60 0 e0 5*80 e0 0 0 0 40 a0 a0 a0 40 0 20 20 20 60 a0
  //   a0 60 0 0 0 60 a0 c0 80 60 4*0 60 40 40 50
endmodule

module BCD (
  input  [11:0] Address,
  input  Select,
  output [7:0] Data,
  output [11:0] Size
);

  ROM #(.addrWidth(12)) rom_1 (.addr(Address), .data(Data), .sel(Select));

  assign Size = 12'h12c;

  // Notes on the sheet:
  //   contents of rom_1 (hex, n*v repeats v):
  //   0 e0 a2 24 f0 65 89 0 a2 25 f9 33 f3 65 6e 1 6d 1 f0 29 de d5 7e 5 f1 29 de d5 7e 5 f2 29 de d5 12
  //   22 ff
endmodule
