// Logisim project mini_chip8_reg.circ as structural Verilog: 4 circuits, main circuit REGI16
module REGI16 (
  input  [7:0] DE,
  input  H,
  input  select,
  input  clear,
  input  storeX,
  input  loadX,
  input  loadY,
  input  [3:0] AX,
  input  [3:0] AY,
  input  [7:0] DM,
  input  storeM,
  output [7:0] D0,
  output [7:0] DX,
  output [7:0] DY
);

  wire decoder_1_out0, decoder_1_out1, decoder_1_out2, decoder_1_out3, decoder_2_out0, decoder_2_out1,
       decoder_2_out2, decoder_2_out3, decoder_3_out0, decoder_3_out1, decoder_3_out2, decoder_3_out3;
  wire [7:0] reg4_1_d0, reg4_1_dx, reg4_1_dy, reg4_2_d0, reg4_2_dx, reg4_2_dy, reg4_3_d0, reg4_3_dx,
       reg4_3_dy, reg4_4_d0, reg4_4_dx, reg4_4_dy;

  Decoder #(.select(2), .disabled(0)) decoder_1 (
    .out0(decoder_1_out0), .out1(decoder_1_out1), .out2(decoder_1_out2), .out3(decoder_1_out3),
    .sel(AX[3:2]), .en(storeX));
  Decoder #(.select(2), .disabled(0)) decoder_2 (
    .out0(decoder_2_out0), .out1(decoder_2_out1), .out2(decoder_2_out2), .out3(decoder_2_out3),
    .sel(AX[3:2]), .en(loadX));
  Decoder #(.select(2), .disabled(0)) decoder_3 (
    .out0(decoder_3_out0), .out1(decoder_3_out1), .out2(decoder_3_out2), .out3(decoder_3_out3),
    .sel(AY[3:2]), .en(loadY));
  REG4 reg4_1 (
    .DE(DE), .AX(AX[1:0]), .AY(AY[1:0]), .H(H), .storeX(decoder_1_out0), .loadX(decoder_2_out0),
    .loadY(decoder_3_out0), .select(select), .clear(clear), .DM({8{1'b0}}), .storeM(1'b0), .D0(reg4_1_d0),
    .DX(reg4_1_dx), .DY(reg4_1_dy));
  REG4 reg4_2 (
    .DE(DE), .AX(AX[1:0]), .AY(AY[1:0]), .H(H), .storeX(decoder_1_out1), .loadX(decoder_2_out1),
    .loadY(decoder_3_out1), .select(select), .clear(clear), .DM({8{1'b0}}), .storeM(1'b0), .D0(reg4_2_d0),
    .DX(reg4_2_dx), .DY(reg4_2_dy));
  REG4 reg4_3 (
    .DE(DE), .AX(AX[1:0]), .AY(AY[1:0]), .H(H), .storeX(decoder_1_out2), .loadX(decoder_2_out2),
    .loadY(decoder_3_out2), .select(select), .clear(clear), .DM({8{1'b0}}), .storeM(1'b0), .D0(reg4_3_d0),
    .DX(reg4_3_dx), .DY(reg4_3_dy));
  REG4 reg4_4 (
    .DE(DE), .AX(AX[1:0]), .AY(AY[1:0]), .H(H), .storeX(decoder_1_out3), .loadX(decoder_2_out3),
    .loadY(decoder_3_out3), .select(select), .clear(clear), .DM(DM), .storeM(storeM), .D0(reg4_4_d0),
    .DX(reg4_4_dx), .DY(reg4_4_dy));
  assign D0 = reg4_1_d0 | reg4_2_d0 | reg4_3_d0 | reg4_4_d0;  // OR_Gate or_1, 8 bits wide
  assign DX = reg4_1_dx | reg4_2_dx | reg4_3_dx | reg4_4_dx;  // OR_Gate or_2, 8 bits wide
  assign DY = reg4_2_dy | reg4_1_dy | reg4_3_dy | reg4_4_dy;  // OR_Gate or_3, 8 bits wide
endmodule

module REG4 (
  input  [7:0] DE,
  input  [1:0] AX,
  input  [1:0] AY,
  input  H,
  input  storeX,
  input  loadX,
  input  loadY,
  input  select,
  input  clear,
  input  [7:0] DM,
  input  storeM,
  output [7:0] D0,
  output [7:0] DX,
  output [7:0] DY
);

  wire and_1_out, and_2_out, and_3_out, and_6_out, and_7_out, demultiplexer_1_out0, demultiplexer_1_out1,
       demultiplexer_1_out2, demultiplexer_1_out3, not_2_out, or_2_out;
  wire [7:0] and_4_out, and_5_out, bit_extender_1_out, not_1_out, or_1_out, register_2_q, register_3_q,
       register_4_q;

  and and_1 (and_1_out, storeX, select);
  and and_2 (and_2_out, loadX, select);
  and and_3 (and_3_out, loadY, select);
  assign bit_extender_1_out = {{7{storeM}}, storeM};  // Bit_Extender bit_extender_1
  Demultiplexer #(.select(2), .disabled(0)) demultiplexer_1 (
    .out0(demultiplexer_1_out0), .out1(demultiplexer_1_out1), .out2(demultiplexer_1_out2),
    .out3(demultiplexer_1_out3), .in(H), .sel(AX), .en(and_1_out));
  assign and_4_out = DE & not_1_out;  // AND_Gate and_4, 8 bits wide
  assign not_1_out = ~bit_extender_1_out;  // NOT_Gate not_1, 8 bits wide
  assign and_5_out = DM & bit_extender_1_out;  // AND_Gate and_5, 8 bits wide
  not not_2 (not_2_out, storeM);
  assign or_1_out = and_4_out | and_5_out;  // OR_Gate or_1, 8 bits wide
  and and_6 (and_6_out, demultiplexer_1_out3, not_2_out);
  or or_2 (or_2_out, and_6_out, and_7_out);
  and and_7 (and_7_out, storeM, H);
  Register register_1 (.D(DE), .en(select), .Q(D0), .clk(demultiplexer_1_out0), .clr(clear));
  Register register_2 (.D(DE), .en(select), .Q(register_2_q), .clk(demultiplexer_1_out1), .clr(clear));
  Register register_3 (.D(DE), .en(select), .Q(register_3_q), .clk(demultiplexer_1_out2), .clr(clear));
  Register register_4 (.D(or_1_out), .en(select), .Q(register_4_q), .clk(or_2_out), .clr(clear));
  Multiplexer #(.select(2), .width(8), .disabled(0)) multiplexer_1 (
    .in0(D0), .in1(register_2_q), .in2(register_3_q), .in3(register_4_q), .out(DX), .sel(AX), .en(and_2_out));
  Multiplexer #(.select(2), .width(8), .disabled(0)) multiplexer_2 (
    .in0(D0), .in1(register_2_q), .in2(register_3_q), .in3(register_4_q), .out(DY), .sel(AY), .en(and_3_out));
endmodule

module REGI16D (
  input  [7:0] DE,
  input  H,
  input  select,
  input  clear,
  input  storeX,
  input  loadX,
  input  loadY,
  input  [3:0] AX,
  input  [3:0] AY,
  input  [7:0] DM,
  input  storeM,
  output [7:0] D0,
  output [7:0] DX,
  output [7:0] DY,
  output [31:0] R0_3,
  output [31:0] R4_7,
  output [31:0] R8_B,
  output [31:0] RC_F
);

  wire decoder_1_out0, decoder_1_out1, decoder_1_out2, decoder_1_out3, decoder_2_out0, decoder_2_out1,
       decoder_2_out2, decoder_2_out3, decoder_3_out0, decoder_3_out1, decoder_3_out2, decoder_3_out3;
  wire [7:0] reg4d_1_d0, reg4d_1_dx, reg4d_1_dy, reg4d_2_d0, reg4d_2_dx, reg4d_2_dy, reg4d_3_d0, reg4d_3_dx,
       reg4d_3_dy, reg4d_4_d0, reg4d_4_dx, reg4d_4_dy;

  Decoder #(.select(2), .disabled(0)) decoder_1 (
    .out0(decoder_1_out0), .out1(decoder_1_out1), .out2(decoder_1_out2), .out3(decoder_1_out3),
    .sel(AX[3:2]), .en(storeX));
  Decoder #(.select(2), .disabled(0)) decoder_2 (
    .out0(decoder_2_out0), .out1(decoder_2_out1), .out2(decoder_2_out2), .out3(decoder_2_out3),
    .sel(AX[3:2]), .en(loadX));
  Decoder #(.select(2), .disabled(0)) decoder_3 (
    .out0(decoder_3_out0), .out1(decoder_3_out1), .out2(decoder_3_out2), .out3(decoder_3_out3),
    .sel(AY[3:2]), .en(loadY));
  REG4D reg4d_1 (
    .DE(DE), .AX(AX[1:0]), .AY(AY[1:0]), .H(H), .storeX(decoder_1_out0), .loadX(decoder_2_out0),
    .loadY(decoder_3_out0), .select(select), .clear(clear), .DM({8{1'b0}}), .storeM(1'b0), .D0(reg4d_1_d0),
    .DX(reg4d_1_dx), .DY(reg4d_1_dy), .D0_3(R0_3));
  REG4D reg4d_2 (
    .DE(DE), .AX(AX[1:0]), .AY(AY[1:0]), .H(H), .storeX(decoder_1_out1), .loadX(decoder_2_out1),
    .loadY(decoder_3_out1), .select(select), .clear(clear), .DM({8{1'b0}}), .storeM(1'b0), .D0(reg4d_2_d0),
    .DX(reg4d_2_dx), .DY(reg4d_2_dy), .D0_3(R4_7));
  REG4D reg4d_3 (
    .DE(DE), .AX(AX[1:0]), .AY(AY[1:0]), .H(H), .storeX(decoder_1_out2), .loadX(decoder_2_out2),
    .loadY(decoder_3_out2), .select(select), .clear(clear), .DM({8{1'b0}}), .storeM(1'b0), .D0(reg4d_3_d0),
    .DX(reg4d_3_dx), .DY(reg4d_3_dy), .D0_3(R8_B));
  REG4D reg4d_4 (
    .DE(DE), .AX(AX[1:0]), .AY(AY[1:0]), .H(H), .storeX(decoder_1_out3), .loadX(decoder_2_out3),
    .loadY(decoder_3_out3), .select(select), .clear(clear), .DM(DM), .storeM(storeM), .D0(reg4d_4_d0),
    .DX(reg4d_4_dx), .DY(reg4d_4_dy), .D0_3(RC_F));
  assign D0 = reg4d_1_d0 | reg4d_2_d0 | reg4d_3_d0 | reg4d_4_d0;  // OR_Gate or_1, 8 bits wide
  assign DX = reg4d_1_dx | reg4d_2_dx | reg4d_3_dx | reg4d_4_dx;  // OR_Gate or_2, 8 bits wide
  assign DY = reg4d_2_dy | reg4d_1_dy | reg4d_3_dy | reg4d_4_dy;  // OR_Gate or_3, 8 bits wide
endmodule

module REG4D (
  input  [7:0] DE,
  input  [1:0] AX,
  input  [1:0] AY,
  input  H,
  input  storeX,
  input  loadX,
  input  loadY,
  input  select,
  input  clear,
  input  [7:0] DM,
  input  storeM,
  output [7:0] D0,
  output [7:0] DX,
  output [7:0] DY,
  output [31:0] D0_3
);

  wire and_1_out, and_2_out, and_3_out, and_6_out, and_7_out, demultiplexer_1_out0, demultiplexer_1_out1,
       demultiplexer_1_out2, demultiplexer_1_out3, not_2_out, or_2_out;
  wire [7:0] and_4_out, and_5_out, bit_extender_1_out, not_1_out, or_1_out;

  and and_1 (and_1_out, storeX, select);
  and and_2 (and_2_out, loadX, select);
  and and_3 (and_3_out, loadY, select);
  assign bit_extender_1_out = {{7{storeM}}, storeM};  // Bit_Extender bit_extender_1
  Demultiplexer #(.select(2), .disabled(0)) demultiplexer_1 (
    .out0(demultiplexer_1_out0), .out1(demultiplexer_1_out1), .out2(demultiplexer_1_out2),
    .out3(demultiplexer_1_out3), .in(H), .sel(AX), .en(and_1_out));
  assign and_4_out = DE & not_1_out;  // AND_Gate and_4, 8 bits wide
  assign not_1_out = ~bit_extender_1_out;  // NOT_Gate not_1, 8 bits wide
  assign and_5_out = DM & bit_extender_1_out;  // AND_Gate and_5, 8 bits wide
  not not_2 (not_2_out, storeM);
  assign or_1_out = and_4_out | and_5_out;  // OR_Gate or_1, 8 bits wide
  and and_6 (and_6_out, demultiplexer_1_out3, not_2_out);
  or or_2 (or_2_out, and_6_out, and_7_out);
  and and_7 (and_7_out, storeM, H);
  Register register_1 (.D(DE), .en(select), .Q(D0), .clk(demultiplexer_1_out0), .clr(clear));
  Register register_2 (.D(DE), .en(select), .Q(D0_3[15:8]), .clk(demultiplexer_1_out1), .clr(clear));
  Register register_3 (.D(DE), .en(select), .Q(D0_3[23:16]), .clk(demultiplexer_1_out2), .clr(clear));
  Register register_4 (.D(or_1_out), .en(select), .Q(D0_3[31:24]), .clk(or_2_out), .clr(clear));
  Multiplexer #(.select(2), .width(8), .disabled(0)) multiplexer_1 (
    .in0(D0), .in1(D0_3[15:8]), .in2(D0_3[23:16]), .in3(D0_3[31:24]), .out(DX), .sel(AX), .en(and_2_out));
  Multiplexer #(.select(2), .width(8), .disabled(0)) multiplexer_2 (
    .in0(D0), .in1(D0_3[15:8]), .in2(D0_3[23:16]), .in3(D0_3[31:24]), .out(DY), .sel(AY), .en(and_3_out));

  assign D0_3[7:0] = D0;
endmodule
