// Logisim project mini_chip8_savd.circ as structural Verilog: 1 circuit, main circuit SAVD
module SAVD (
  input  H,
  input  T,
  input  clear,
  output S
);

  wire d_ff_1_q, d_ff_1_qn, d_ff_2_q, d_ff_2_qn, or_1_out;

  D_Flip_Flop #(.trigger("falling")) d_ff_1 (
    .clk(H), .D(d_ff_1_qn), .Q(d_ff_1_q), .Qn(d_ff_1_qn), .preset(1'b0), .en(T), .reset(or_1_out));
  D_Flip_Flop d_ff_2 (.clk(H), .D(d_ff_2_qn), .Q(d_ff_2_q), .Qn(d_ff_2_qn), .preset(1'b0), .en(T), .reset(clear));
  or or_1 (or_1_out, d_ff_2_q, clear);
  and and_1 (S, d_ff_1_q, T);
endmodule
