// Logisim project mini_chip8_db.circ as structural Verilog: 5 circuits, main circuit main
module main (
  input  in_1,
  output out_2,
  output C8PIC,
  output BC_test,
  output MAZE,
  output BCD,
  output X_MIRROR,
  output PONG,
  output BREAKOUT,
  output VOITURE
);

  wire and_1_out, and_2_out, and_3_out, button_1_out, chip8_1_gsel, chip8_1_h_2, chip8_1_m, chip8_1_r,
       chip8_1_scs, chip8_1_selr, chip8_1_son, chip8_1_sscp, d_ff_1_q, H_out, MA_out, not_1_out, or_1_out,
       RESET_out;
  wire [4:0] chip8_1_scy, undriven;
  wire [5:0] chip8_1_scx;
  wire [7:0] chip8_1_r0_3, chip8_1_r0_3_2, chip8_1_r0_3_3, chip8_1_r0_3_4, chip8_1_r4_7, chip8_1_r4_7_2,
       chip8_1_r4_7_3, chip8_1_r4_7_4, chip8_1_r8_b, chip8_1_r8_b_2, chip8_1_r8_b_3, chip8_1_r8_b_4,
       chip8_1_rc_f, chip8_1_rc_f_2, chip8_1_rc_f_3, chip8_1_rc_f_4, games_1_game_data, reg_dif_1_out_8,
       reg_dif_1_out_8_2, reg_dif_1_out_8_3, reg_dif_1_out_8_4, reg_dif_1_out_9, reg_dif_1_out_9_2,
       reg_dif_1_out_9_3, reg_dif_1_out_9_4, reg_dif_1_out_11, reg_dif_1_out_11_2, reg_dif_1_out_11_3,
       reg_dif_1_out_11_4;
  wire [11:0] chip8_1_ar, chip8_1_ga, games_1_game_size;
  wire [15:0] chip8_1_opcode;
  wire [31:0] reg_dif_1_out_10;

  Button button_1 (.out(button_1_out));
  Button MA (.out(MA_out));
  Button RESET (.out(RESET_out));
  GAMES games_1 (
    .Select(button_1_out), .Game_Adress(chip8_1_ga), .Game_Select(chip8_1_gsel),
    .Game_Data(games_1_game_data), .Choice({VOITURE, BREAKOUT, PONG, X_MIRROR, BCD, MAZE, BC_test, C8PIC}),
    .Game_Size(games_1_game_size));
  CHIP8 chip8_1 (
    .MA(MA_out), .RESET(RESET_out), .CL(undriven), .SCX(chip8_1_scx), .SCY(chip8_1_scy), .SCS(chip8_1_scs),
    .SSCP(chip8_1_sscp), .GA(chip8_1_ga), .H_2(chip8_1_h_2), .R(chip8_1_r), .GD(games_1_game_data),
    .Gsel(chip8_1_gsel), .SON(chip8_1_son), .LedM(out_2), .in_5(games_1_game_size),
    .R0_3({chip8_1_r0_3_4, chip8_1_r0_3_3, chip8_1_r0_3_2, chip8_1_r0_3}),
    .R4_7({chip8_1_r4_7_4, chip8_1_r4_7_3, chip8_1_r4_7_2, chip8_1_r4_7}),
    .R8_B({chip8_1_r8_b_4, chip8_1_r8_b_3, chip8_1_r8_b_2, chip8_1_r8_b}),
    .RC_F({chip8_1_rc_f_4, chip8_1_rc_f_3, chip8_1_rc_f_2, chip8_1_rc_f}), .AR(chip8_1_ar),
    .OPCODE(chip8_1_opcode), .SELR(chip8_1_selr), .M(chip8_1_m), .H(or_1_out));
  // ScreenColor screencolor_1: pin names not known; wires that end beside it: chip8_1_r, chip8_1_scs, chip8_1_sscp, chip8_1_h_2, chip8_1_scx, chip8_1_scy
  // AudioBip audiobip_1: pin names not known; wires that end beside it: chip8_1_son
  // Keyboard keyboard_1: pin names not known
  not not_1 (not_1_out, chip8_1_m);
  Clock H (.out(H_out));
  D_Flip_Flop #(.trigger("high")) d_ff_1 (
    .clk(or_1_out), .D(chip8_1_selr), .Q(d_ff_1_q), .preset(1'b0), .en(1'b1), .reset(RESET_out));  // open: Qn
  and and_1 (and_1_out, not_1_out, H_out);
  or or_1 (or_1_out, and_1_out, and_2_out);
  and and_2 (and_2_out, H_out, chip8_1_m, in_1);
  and and_3 (and_3_out, d_ff_1_q, chip8_1_m);
  // Probe on chip8_1_r0_3
  // Probe on chip8_1_r0_3_2
  // Probe on chip8_1_r0_3_3
  // Probe on chip8_1_r0_3_4
  // Probe on chip8_1_r4_7
  // Probe on chip8_1_r4_7_2
  // Probe on chip8_1_r4_7_3
  // Probe on chip8_1_r4_7_4
  // Probe on chip8_1_r8_b
  // Probe on chip8_1_r8_b_2
  // Probe on chip8_1_r8_b_3
  // Probe on chip8_1_r8_b_4
  // Probe on chip8_1_rc_f
  // Probe on chip8_1_rc_f_2
  // Probe on chip8_1_rc_f_3
  // Probe on chip8_1_rc_f_4
  // Probe on chip8_1_ar
  // Probe on chip8_1_ar
  // Probe on chip8_1_ar
  // Probe on chip8_1_ar
  // Probe on chip8_1_opcode
  // Probe on chip8_1_opcode
  // Probe on chip8_1_opcode
  // Probe on chip8_1_opcode
  // Probe on reg_dif_1_out_11
  // Probe on reg_dif_1_out_11_2
  // Probe on reg_dif_1_out_11_3
  // Probe on reg_dif_1_out_11_4
  // Probe on reg_dif_1_out_10[7:0]
  // Probe on reg_dif_1_out_10[15:8]
  // Probe on reg_dif_1_out_10[23:16]
  // Probe on reg_dif_1_out_10[31:24]
  // Probe on reg_dif_1_out_9
  // Probe on reg_dif_1_out_9_2
  // Probe on reg_dif_1_out_9_3
  // Probe on reg_dif_1_out_9_4
  // Probe on reg_dif_1_out_8
  // Probe on reg_dif_1_out_8_2
  // Probe on reg_dif_1_out_8_3
  // Probe on reg_dif_1_out_8_4
  REG_DIF reg_dif_1 (
    .in_1({chip8_1_rc_f_4, chip8_1_rc_f_3, chip8_1_rc_f_2, chip8_1_rc_f}),
    .in_2({chip8_1_r8_b_4, chip8_1_r8_b_3, chip8_1_r8_b_2, chip8_1_r8_b}),
    .in_3({chip8_1_r4_7_4, chip8_1_r4_7_3, chip8_1_r4_7_2, chip8_1_r4_7}),
    .in_4({chip8_1_r0_3_4, chip8_1_r0_3_3, chip8_1_r0_3_2, chip8_1_r0_3}), .in_6(or_1_out), .in_7(RESET_out),
    .out_8({reg_dif_1_out_8_4, reg_dif_1_out_8_3, reg_dif_1_out_8_2, reg_dif_1_out_8}),
    .out_9({reg_dif_1_out_9_4, reg_dif_1_out_9_3, reg_dif_1_out_9_2, reg_dif_1_out_9}),
    .out_10(reg_dif_1_out_10),
    .out_11({reg_dif_1_out_11_4, reg_dif_1_out_11_3, reg_dif_1_out_11_2, reg_dif_1_out_11}), .in_5(and_3_out));

  // Notes on the sheet:
  //   in_1: pull=up
endmodule

module CPU (
  input  [7:0] DR,
  input  enable,
  input  [4:0] CL,
  input  SCP,
  input  H,
  input  clear,
  output [15:0] opcode,
  output [11:0] PC,
  output [7:0] CMPG,
  output [11:0] I,
  output [15:0] CMPSON,
  output SON,
  output [3:0] nbrsaut,
  output [11:0] saut,
  output [11:0] AR,
  output [7:0] DR_2,
  output SR,
  output RE,
  output [5:0] SCX,
  output [4:0] SCY,
  output SCstore,
  output SSCP,
  output [31:0] R0_3,
  output [31:0] R4_7,
  output [31:0] R8_B,
  output [31:0] RC_F
);

  wire alu_1_ec, alu_1_scmpgame, alu_1_scmpson, alu_1_si, alu_1_snbrsaut, alu_1_spc, alu_1_ssaut, alu_1_svf,
       alu_1_svx, and_1_out, cpm_1_end, cpm_1_t1, cpm_1_t2, d_ff_1_q, d_ff_1_qn, dec_1__00e0, dec_1__00ee,
       dec_1__0nnn, dec_1__1nnn, dec_1__2nnn, dec_1__3xkk, dec_1__4xkk, dec_1__5xy0, dec_1__6xkk,
       dec_1__7xkk, dec_1__8x0e, dec_1__8x06, dec_1__8xy0, dec_1__8xy1, dec_1__8xy2, dec_1__8xy3,
       dec_1__8xy4, dec_1__8xy5, dec_1__8xy7, dec_1__9xy0, dec_1_annn, dec_1_bnnn, dec_1_cxkk, dec_1_dxyk,
       dec_1_ex9e, dec_1_exa1, dec_1_fx0a, dec_1_fx1e, dec_1_fx07, dec_1_fx15, dec_1_fx18, dec_1_fx29,
       dec_1_fx33, dec_1_fx55, dec_1_fx65, loadr_1_end, loadr_1_spc, not_1_out, or_1_out, or_2_out, or_3_out,
       or_5_out;
  wire [3:0] alu_1_ax, alu_1_ay, alu_1_nbrsaut_2, alu_1_nc, dec_1_ax, dec_1_ay, dec_1_k;
  wire [7:0] alu_1_cmpgame_2, alu_1_vf, alu_1_vx_2, dec_1_kk, regi16d_1_d0, regi16d_1_dx, regi16d_1_dy;
  wire [11:0] alu_1_ar, alu_1_i_2, alu_1_pc_2, alu_1_saut_2, and_2_out, and_3_out, bit_extender_1_out,
       dec_1_nnn, loadr_1_pc_2, not_2_out, or_4_out;
  wire [15:0] alu_1_cmpson_2;

  not not_1 (not_1_out, enable);
  and and_1 (and_1_out, enable, d_ff_1_qn);
  or or_1 (or_1_out, not_1_out, clear);
  or or_2 (or_2_out, cpm_1_end, or_1_out);
  loadR loadr_1 (
    .DR(DR), .enable(and_1_out), .H(H), .clear(or_2_out), .PC(PC), .opcode(opcode), .\end (loadr_1_end),
    .SPC(loadr_1_spc), .PC_2(loadr_1_pc_2));
  DEC dec_1 (
    .enable(loadr_1_end), .opcode(opcode), .AX(dec_1_ax), .AY(dec_1_ay), .K(dec_1_k), .KK(dec_1_kk),
    .NNN(dec_1_nnn), ._00E0(dec_1__00e0), ._00EE(dec_1__00ee), ._0NNN(dec_1__0nnn), ._1NNN(dec_1__1nnn),
    ._2NNN(dec_1__2nnn), .ANNN(dec_1_annn), .BNNN(dec_1_bnnn), ._3XKK(dec_1__3xkk), ._4XKK(dec_1__4xkk),
    ._6XKK(dec_1__6xkk), ._7XKK(dec_1__7xkk), .CXKK(dec_1_cxkk), ._5XY0(dec_1__5xy0), ._8XY0(dec_1__8xy0),
    ._8XY1(dec_1__8xy1), ._8XY2(dec_1__8xy2), ._8XY3(dec_1__8xy3), ._8XY4(dec_1__8xy4), ._8XY5(dec_1__8xy5),
    ._8XY7(dec_1__8xy7), ._9XY0(dec_1__9xy0), .DXYK(dec_1_dxyk), ._8X06(dec_1__8x06), ._8X0E(dec_1__8x0e),
    .EX9E(dec_1_ex9e), .EXA1(dec_1_exa1), .FX07(dec_1_fx07), .FX0A(dec_1_fx0a), .FX15(dec_1_fx15),
    .FX18(dec_1_fx18), .FX1E(dec_1_fx1e), .FX29(dec_1_fx29), .FX33(dec_1_fx33), .FX55(dec_1_fx55),
    .FX65(dec_1_fx65));
  ALU alu_1 (
    .X(dec_1_ax), .Y(dec_1_ay), .VX(regi16d_1_dx), .VY(regi16d_1_dy), .saut(saut), .NNN(dec_1_nnn), .PC(PC),
    .nbrsaut(nbrsaut), .KK(dec_1_kk), ._0NNN(dec_1__0nnn), ._00E0(dec_1__00e0), ._00EE(dec_1__00ee),
    ._1NNN(dec_1__1nnn), ._2NNN(dec_1__2nnn), ._3XKK(dec_1__3xkk), ._4XKK(dec_1__4xkk), ._5XY0(dec_1__5xy0),
    ._6XKK(dec_1__6xkk), ._7XKK(dec_1__7xkk), ._8X06(dec_1__8x06), ._8X0E(dec_1__8x0e), ._8XY0(dec_1__8xy0),
    ._8XY1(dec_1__8xy1), ._8XY2(dec_1__8xy2), ._8XY3(dec_1__8xy3), ._8XY4(dec_1__8xy4), ._8XY5(dec_1__8xy5),
    ._8XY7(dec_1__8xy7), ._9XY0(dec_1__9xy0), .ANNN(dec_1_annn), .BNNN(dec_1_bnnn), .CXKK(dec_1_cxkk),
    .DXYK(dec_1_dxyk), .EX9E(dec_1_ex9e), .EXA1(dec_1_exa1), .FX07(dec_1_fx07), .FX0A(dec_1_fx0a),
    .FX15(dec_1_fx15), .FX18(dec_1_fx18), .FX1E(dec_1_fx1e), .FX29(dec_1_fx29), .FX33(dec_1_fx33),
    .FX55(dec_1_fx55), .FX65(dec_1_fx65), .SCP(SCP), .K(dec_1_k), .CMPGAME(CMPG), .V0(regi16d_1_d0), .CL(CL),
    .I(I), .DR(DR), .H(H), .T1(cpm_1_t1), .T2(cpm_1_t2), .RE(RE), .Snbrsaut(alu_1_snbrsaut),
    .nbrsaut_2(alu_1_nbrsaut_2), .saut_2(alu_1_saut_2), .Ssaut(alu_1_ssaut), .VF(alu_1_vf), .SVF(alu_1_svf),
    .AY(alu_1_ay), .PC_2(alu_1_pc_2), .SPC(alu_1_spc), .I_2(alu_1_i_2), .SI(alu_1_si), .AR(alu_1_ar),
    .SCX(SCX), .SCY(SCY), .SCstore(SCstore), .SSCP(SSCP), .CMPGAME_2(alu_1_cmpgame_2),
    .SCMPGAME(alu_1_scmpgame), .CMPSON_2(alu_1_cmpson_2), .SCMPSON(alu_1_scmpson), .DR_2(DR_2), .SR(SR),
    .VX_2(alu_1_vx_2), .SVX(alu_1_svx), .AX(alu_1_ax), .EC(alu_1_ec), .NC(alu_1_nc), .SON(SON),
    .CMPSON(CMPSON));
  CPM cpm_1 (
    .enable(d_ff_1_q), .H(H), .NC(alu_1_nc), .EC(alu_1_ec), .T1(cpm_1_t1), .T2(cpm_1_t2), .\end (cpm_1_end));  // open: T0, T3, T4, T5, T6, T7
  D_Flip_Flop d_ff_1 (
    .clk(loadr_1_end), .D(1'b1), .Q(d_ff_1_q), .Qn(d_ff_1_qn), .preset(1'b0), .en(1'b1), .reset(or_3_out));
  or or_3 (or_3_out, or_1_out, cpm_1_end);
  assign or_4_out = loadr_1_pc_2 | alu_1_pc_2;  // OR_Gate or_4, 12 bits wide
  or or_5 (or_5_out, alu_1_spc, loadr_1_spc);
  Register #(.width(12)) u_PC (.D(or_4_out), .en(or_5_out), .Q(PC), .clk(H), .clr(or_1_out));
  Register compteurJeu (.D(alu_1_cmpgame_2), .en(alu_1_scmpgame), .Q(CMPG), .clk(H), .clr(or_1_out));
  Register #(.width(12)) I_adresse_memoire (.D(alu_1_i_2), .en(alu_1_si), .Q(I), .clk(H), .clr(or_1_out));
  REGI16D regi16d_1 (
    .DE(alu_1_vx_2), .AX(alu_1_ax), .AY(alu_1_ay), .H(H), .storeX(alu_1_svx), .loadX(1'b1), .loadY(1'b1),
    .select(1'b1), .clear(or_1_out), .DX(regi16d_1_dx), .DY(regi16d_1_dy), .R0_3(R0_3), .R4_7(R4_7),
    .R8_B(R8_B), .RC_F(RC_F), .D0(regi16d_1_d0), .DM(alu_1_vf), .storeM(alu_1_svf));
  assign bit_extender_1_out = {{11{d_ff_1_qn}}, d_ff_1_qn};  // Bit_Extender bit_extender_1
  Register #(.width(16)) compteurSon (.D(alu_1_cmpson_2), .en(alu_1_scmpson), .Q(CMPSON), .clk(H), .clr(or_1_out));
  Register #(.width(4)) u_nbrsaut (.D(alu_1_nbrsaut_2), .en(alu_1_snbrsaut), .Q(nbrsaut), .clk(H), .clr(or_1_out));
  RAM #(.addrWidth(4), .dataWidth(12), .bus("separate")) ram_1 (
    .addr(nbrsaut), .din(alu_1_saut_2), .data(saut), .str(alu_1_ssaut), .sel(1'b1), .clk(H), .ld(1'b1),
    .clr(or_1_out));
  assign not_2_out = ~bit_extender_1_out;  // NOT_Gate not_2, 12 bits wide
  assign and_2_out = bit_extender_1_out & PC;  // AND_Gate and_2, 12 bits wide
  assign and_3_out = alu_1_ar & not_2_out;  // AND_Gate and_3, 12 bits wide
  assign AR = and_2_out | and_3_out;  // OR_Gate or_6, 12 bits wide

  // Notes on the sheet:
  //   saut
endmodule

module CHIP8 (
  input  H,
  input  MA,
  input  RESET,
  input  [4:0] CL,
  input  [11:0] in_5,
  input  [7:0] GD,
  output LedM,
  output R,
  output SCS,
  output SSCP,
  output H_2,
  output [5:0] SCX,
  output [4:0] SCY,
  output [11:0] GA,
  output Gsel,
  output SON,
  output M,
  output [15:0] OPCODE,
  output [11:0] AR,
  output [31:0] R0_3,
  output SELR,
  output [31:0] R4_7,
  output [31:0] R8_B,
  output [31:0] RC_F
);

  wire cpu_1_re, cpu_1_scstore, cpu_1_sscp, graf_1_do, graf_1_endi, ma_1_ma_2, ma_1_r, or_1_out,
       transferram_1_p6, transferram_1_p10, transferram_1_p14, transferram_1_p15, transferram_1_p17,
       transferram_1_p21;
  wire [3:0] cpu_1_nbrsaut;
  wire [4:0] cpu_1_scy;
  wire [5:0] cpu_1_scx;
  wire [7:0] cpu_1_cmpg, ram_1_data, transferram_1_p4, transferram_1_p11, transferram_1_p13;
  wire [8:0] transferram_1_p9;
  wire [11:0] cpu_1_i, cpu_1_pc, cpu_1_saut, transferram_1_p5;
  wire [15:0] cpu_1_cmpson;

  MA ma_1 (.MA(MA), .RESET(RESET), .LedM(LedM), .MA_2(ma_1_ma_2), .R(ma_1_r));
  // TransferRam transferram_1: pin names not known; wires that end beside it: H, ma_1_ma_2, ma_1_r, transferram_1_p4, transferram_1_p5, transferram_1_p6, 1'b1, in_5, transferram_1_p9, transferram_1_p10, transferram_1_p11, AR, transferram_1_p13, transferram_1_p14, transferram_1_p15, SELR, transferram_1_p17, GA, Gsel, GD, transferram_1_p21
  ROM #(.addrWidth(9)) rom_1 (.addr(transferram_1_p9), .data(transferram_1_p11), .sel(transferram_1_p10));
  RAM #(.addrWidth(12), .bus("separate")) ram_1 (
    .addr(AR), .din(transferram_1_p13), .data(ram_1_data), .str(transferram_1_p14), .sel(transferram_1_p15),
    .clk(SELR), .ld(1'b1), .clr(transferram_1_p17));
  and and_1 (M, graf_1_endi, transferram_1_p21);
  // Probe on OPCODE
  // Probe on OPCODE
  // Probe on OPCODE
  // Probe on OPCODE
  CPU cpu_1 (
    .DR(ram_1_data), .enable(M), .CL(CL), .SCP(graf_1_do), .H(H), .clear(ma_1_r), .opcode(OPCODE),
    .AR(transferram_1_p5), .DR_2(transferram_1_p4), .SR(transferram_1_p6), .RE(cpu_1_re), .SCX(cpu_1_scx),
    .SCY(cpu_1_scy), .SCstore(cpu_1_scstore), .SSCP(cpu_1_sscp), .R0_3(R0_3), .R4_7(R4_7), .R8_B(R8_B),
    .RC_F(RC_F), .nbrsaut(cpu_1_nbrsaut), .PC(cpu_1_pc), .saut(cpu_1_saut), .I(cpu_1_i), .CMPG(cpu_1_cmpg),
    .CMPSON(cpu_1_cmpson), .SON(SON));
  // Probe on cpu_1_pc
  // Probe on cpu_1_pc
  // Probe on cpu_1_pc
  // Probe on cpu_1_pc
  // Probe on cpu_1_i
  // Probe on cpu_1_i
  // Probe on cpu_1_i
  // Probe on cpu_1_i
  GRAF graf_1 (
    .DO(graf_1_do), .AL(cpu_1_scx), .AL_2(SCX), .AC(cpu_1_scy), .AC_2(SCY), .E(ma_1_ma_2), .M(M), .clear(R),
    .R(or_1_out), .Enable(SSCP), .D(cpu_1_sscp), .DIS(SCS), .H_2(H_2), .H(H), .Store(cpu_1_scstore),
    .ENDI(graf_1_endi));
  or or_1 (or_1_out, cpu_1_re, ma_1_r);
  // Probe on cpu_1_saut
  // Probe on cpu_1_saut
  // Probe on cpu_1_saut
  // Probe on cpu_1_saut
  // Probe on cpu_1_cmpson
  // Probe on cpu_1_cmpson
  // Probe on cpu_1_cmpson
  // Probe on cpu_1_cmpson
  // Probe on cpu_1_nbrsaut
  // Probe on cpu_1_nbrsaut
  // Probe on cpu_1_nbrsaut
  // Probe on cpu_1_nbrsaut
  // Probe on cpu_1_cmpg
  // Probe on cpu_1_cmpg
  // Probe on cpu_1_cmpg
  // Probe on cpu_1_cmpg
  // Probe on R0_3[31:24]
  // Probe on R0_3[31:24]
  // Probe on R0_3[31:24]
  // Probe on R0_3[31:24]
  // Probe on R4_7[31:24]
  // Probe on R4_7[31:24]
  // Probe on R4_7[31:24]
  // Probe on R4_7[31:24]
  // Probe on R8_B[31:24]
  // Probe on R8_B[31:24]
  // Probe on R8_B[31:24]
  // Probe on R8_B[31:24]
  // Probe on RC_F[31:24]
  // Probe on RC_F[31:24]
  // Probe on RC_F[31:24]
  // Probe on RC_F[31:24]
  // Probe on R0_3[23:16]
  // Probe on R0_3[23:16]
  // Probe on R0_3[23:16]
  // Probe on R0_3[23:16]
  // Probe on R4_7[23:16]
  // Probe on R4_7[23:16]
  // Probe on R4_7[23:16]
  // Probe on R4_7[23:16]
  // Probe on R8_B[23:16]
  // Probe on R8_B[23:16]
  // Probe on R8_B[23:16]
  // Probe on R8_B[23:16]
  // Probe on RC_F[23:16]
  // Probe on RC_F[23:16]
  // Probe on RC_F[23:16]
  // Probe on RC_F[23:16]
  // Probe on R0_3[15:8]
  // Probe on R0_3[15:8]
  // Probe on R0_3[15:8]
  // Probe on R0_3[15:8]
  // Probe on R4_7[15:8]
  // Probe on R4_7[15:8]
  // Probe on R4_7[15:8]
  // Probe on R4_7[15:8]
  // Probe on R8_B[15:8]
  // Probe on R8_B[15:8]
  // Probe on R8_B[15:8]
  // Probe on R8_B[15:8]
  // Probe on RC_F[15:8]
  // Probe on RC_F[15:8]
  // Probe on RC_F[15:8]
  // Probe on RC_F[15:8]
  // Probe on R0_3[7:0]
  // Probe on R0_3[7:0]
  // Probe on R0_3[7:0]
  // Probe on R0_3[7:0]
  // Probe on R4_7[7:0]
  // Probe on R4_7[7:0]
  // Probe on R4_7[7:0]
  // Probe on R4_7[7:0]
  // Probe on R8_B[7:0]
  // Probe on R8_B[7:0]
  // Probe on R8_B[7:0]
  // Probe on R8_B[7:0]
  // Probe on RC_F[7:0]
  // Probe on RC_F[7:0]
  // Probe on RC_F[7:0]
  // Probe on RC_F[7:0]

  // Notes on the sheet:
  //   MARCHE / ARRET
  //   CLAVIER
  //   RAM
  //   ROM GAME CHIP8
  //   ROM (BIOS)
  //   contents of rom_1 (hex, n*v repeats v):
  //   12 0 0 0 f0 90 90 90 f0 20 60 20 20 70 f0 10 f0 80 f0 f0 10 f0 10 f0 90 90 f0 10 10 f0 80 f0 10 f0
  //   f0 80 f0 90 f0 f0 10 20 40 40 f0 90 f0 90 f0 f0 90 f0 10 f0 f0 90 f0 90 90 e0 90 e0 90 e0 f0 80 80
  //   80 f0 e0 90 90 90 e0 f0 80 f0 80 f0 f0 80 f0 80 80
  //   OPCODE
  //   CPU
  //   PC
  //   I
  //   CMPSON
  //   AUDIO
  //   saut
  //   CMPG
  //   VIDEO
  //   nbrsaut
  //   R3
  //   R7
  //   RB
  //   RF
  //   R2
  //   R6
  //   RA
  //   RE
  //   R1
  //   R5
  //   R9
  //   RD
  //   R0
  //   R4
  //   R8
  //   RC
endmodule

module GRAF (
  input  [5:0] AL,
  input  [4:0] AC,
  input  Store,
  input  D,
  input  H,
  input  R,
  input  M,
  input  E,
  output clear,
  output DIS,
  output Enable,
  output H_2,
  output [4:0] AC_2,
  output [5:0] AL_2,
  output DO,
  output ENDI
);

  wire imagescreen_1_p11, imagescreen_1_p12, imagescreen_1_p19, imagescreen_1_p20, imagescreen_1_p21,
       imagescreen_1_p22, imagescreen_1_p23;
  wire [11:0] imageromscreen_1_p8;
  wire [23:0] rom_1_data;

  // ImageScreen imagescreen_1: pin names not known; wires that end beside it: AL, AC, Store, D, DO, H, R, M, E, ENDI, imagescreen_1_p11, imagescreen_1_p12, clear, DIS, Enable, H_2, AC_2, AL_2, imagescreen_1_p19, imagescreen_1_p20, imagescreen_1_p21, imagescreen_1_p22, imagescreen_1_p23
  ROM #(.addrWidth(12), .dataWidth(24)) rom_1 (.addr(imageromscreen_1_p8), .data(rom_1_data), .sel(1'b1));
  // ImageRomScreen imageromscreen_1: pin names not known; wires that end beside it: rom_1_data, imagescreen_1_p11, imagescreen_1_p12, imagescreen_1_p21, imagescreen_1_p20, imagescreen_1_p22, imagescreen_1_p23, imageromscreen_1_p8
  // Collision collision_1: pin names not known; wires that end beside it: AL_2, AC_2, H_2, Enable, DIS, clear, imagescreen_1_p19

  // Notes on the sheet:
  //   contents of rom_1 (hex, n*v repeats v):
  //   40 20 121*0 6*ffffff 26*0 ffffff 0 0 ffffff 28*0 ffffff 0 0 ffffff 17*0 ffffff ffffff ffffff 8*0
  //   ffffff 0 0 ffffff 16*0 6*ffffff 7*0 ffffff ffffff 16*0 ffffff ffffff 0 0 0 ffffff ffffff ffffff 23*0
  //   ffffff ffffff 6*0 ffffff ffffff 5*0 4*ffffff 12*0 ffffff ffffff 8*0 ffffff ffffff 0 0 0 ffffff 4*0
  //   ffffff 11*0 ffffff 10*0 ffffff 0 0 0 ffffff 4*0 ffffff 11*0 ffffff 10*0 ffffff 0 0 0 ffffff 4*0
  //   ffffff 0 0 6*ffffff 0 0 0 ffffff 10*0 ffffff 4*0 ffffff 0 0 ffffff 8*0 ffffff 0 0 0 ffffff ffffff
  //   ffffff 6*0 ffffff ffffff ffffff 16*0 ffffff 4*0 ffffff ffffff 6*0 ffffff ffffff 4*0 ffffff 12*0
  //   ffffff 18*0 ffffff 12*0 ffffff 0 0 0 ffffff 10*0 ffffff 0 0 0 6*ffffff 11*0 12*ffffff 0 0 0 ffffff
  //   7*0 5*ffffff 4*0 12*ffffff 0 0 0 ffffff 12*0 ffffff 0 0 0 ffffff 4*0 ffffff 5*0 ffffff 16*0 ffffff
  //   8*0 ffffff 9*0 6*ffffff 7*0 ffffff 8*0 ffffff 9*0 ffffff 0 0 ffffff 4*0 5*ffffff 9*0 ffffff 9*0
  //   ffffff 0 0 ffffff 18*0 ffffff 9*0 ffffff 0 0 ffffff ffffff 0 0 0 6*ffffff 0 0 0 ffffff 4*0 ffffff
  //   5*0 ffffff 4*0 ffffff ffffff 0 0 ffffff 0 0 ffffff 4*0 ffffff 0 0 0 12*ffffff 11*0 ffffff 4*0 ffffff
  //   0 0 0 12*ffffff 4*0 4*ffffff 0 0 0 ffffff 4*0 ffffff 0 0 0 ffffff 10*0 ffffff 0 0 0 ffffff 4*0
  //   ffffff 0 0 0 4*ffffff 19*0 ffffff 4*0 ffffff 11*0 ffffff 10*0 ffffff 0 0 0 ffffff 4*0 ffffff 0 0 0
  //   4*ffffff 4*0 12*ffffff 4*0 4*ffffff 0 0 0 ffffff 4*0 ffffff 0 0 0 12*ffffff 11*0 ffffff 4*0 ffffff 0
  //   0 0 ffffff 10*0 ffffff 0 0 0 6*ffffff 0 0 ffffff 4*0 ffffff 18*0 ffffff ffffff 7*0 4*ffffff 4*0
  //   ffffff 10*0 ffffff 5*0 ffffff ffffff 13*0 12*ffffff 7*0 ffffff ffffff 0 0 ffffff ffffff 7*0
  //   12*ffffff 0 0 0 6*ffffff 4*0 ffffff ffffff 5*0 ffffff 4*0 ffffff 5*0 ffffff 15*0 ffffff ffffff 0 0 0
  //   ffffff 4*0 ffffff 9*0 ffffff 4*0 ffffff 4*0 ffffff ffffff 5*0 ffffff 4*0 ffffff 9*0 6*ffffff 0 0
  //   ffffff ffffff 7*0 ffffff ffffff 0 0 ffffff ffffff 9*0 ffffff 4*0 ffffff 12*0 4*ffffff 18*0 ffffff
  //   4*0 ffffff 5*0 ffffff ffffff 12*0 4*ffffff 0 0 0 6*ffffff 18*0 ffffff 4*0 ffffff 0 0 ffffff 4*0
  //   ffffff 8*0 ffffff ffffff 8*0 ffffff 4*0 ffffff 16*0 ffffff ffffff 8*0 ffffff 0 0 0 ffffff ffffff 0 0
  //   0 4*ffffff 9*0 ffffff ffffff 9*0 5*ffffff 0 0 ffffff 4*0 ffffff 8*0 ffffff ffffff 16*0 ffffff 4*0
  //   ffffff 18*0 5*ffffff 0 0 0 ffffff 4*0 ffffff 5*0 ffffff ffffff 0 0 0 ffffff ffffff ffffff 10*0
  //   ffffff 0 0 0 ffffff 0 0 ffffff 5*0 4*ffffff 0 5*ffffff 9*0 ffffff 11*0 ffffff ffffff 0 0 ffffff
  //   ffffff ffffff 0 0 0 ffffff ffffff 8*0 ffffff 11*0 ffffff 4*0 ffffff 5*0 ffffff 0 0 0 5*ffffff 12*0
  //   ffffff 4*0 ffffff 5*0 ffffff 20*0 ffffff ffffff 0 0 ffffff ffffff ffffff 0 0 0 ffffff ffffff 0 0 0
  //   6*ffffff 12*0 4*ffffff 0 5*ffffff 4*0 ffffff 0 0 ffffff 0 ffffff 13*0 ffffff ffffff 0 0 0 ffffff
  //   ffffff ffffff 5*0 ffffff 0 0 ffffff 0 ffffff 26*0 ffffff 0 0 ffffff 0 ffffff 26*0 ffffff 4*0 ffffff
endmodule

module REG_DIF (
  input  [31:0] in_1,
  input  [31:0] in_2,
  input  [31:0] in_3,
  input  [31:0] in_4,
  input  in_5,
  input  in_6,
  input  in_7,
  output [31:0] out_8,
  output [31:0] out_9,
  output [31:0] out_10,
  output [31:0] out_11
);

  Register #(.width(32)) register_1 (.D(in_1), .en(in_5), .Q(out_8), .clk(in_6), .clr(in_7));
  Register #(.width(32)) register_2 (.D(in_2), .en(in_5), .Q(out_9), .clk(in_6), .clr(in_7));
  Register #(.width(32)) register_3 (.D(in_3), .en(in_5), .Q(out_10), .clk(in_6), .clr(in_7));
  Register #(.width(32)) register_4 (.D(in_4), .en(in_5), .Q(out_11), .clk(in_6), .clr(in_7));
endmodule
